// Logisim project Abacus_181.circ as structural Verilog: 27 circuits, main circuit mainInternal
module mainInternal (
  input  PWR,
  input  CLK_Pulse,
  input  CLK_Mode,
  input  MAR_AddrSW11,
  input  MAR_AddrSW10,
  input  MAR_AddrSW9,
  input  MAR_AddrSW8,
  input  MAR_AddrSW7,
  input  MAR_AddrSW6,
  input  MAR_AddrSW5,
  input  MAR_AddrSW4,
  input  MAR_AddrSW3,
  input  MAR_AddrSW2,
  input  MAR_AddrSW1,
  input  MAR_AddrSW0,
  input  MAR_Mode,
  input  RAM_Clear,
  input  RAM_ProgOK,
  input  RAM_ProgSW15,
  input  RAM_ProgSW14,
  input  RAM_ProgSW13,
  input  RAM_ProgSW12,
  input  RAM_ProgSW11,
  input  RAM_ProgSW10,
  input  RAM_ProgSW9,
  input  RAM_ProgSW8,
  input  RAM_ProgSW7,
  input  RAM_ProgSW6,
  input  RAM_ProgSW5,
  input  RAM_ProgSW4,
  input  RAM_ProgSW3,
  input  RAM_ProgSW2,
  input  RAM_ProgSW1,
  input  RAM_ProgSW0,
  input  OUT_Hex,
  input  OUT_Twos,
  input  MasterReset,
  output PWR_LED,
  output CLK_LED,
  output PC_LED11,
  output PC_LED10,
  output PC_LED9,
  output PC_LED8,
  output PC_LED7,
  output PC_LED6,
  output PC_LED5,
  output PC_LED4,
  output PC_LED3,
  output PC_LED2,
  output PC_LED1,
  output PC_LED0,
  output CLK_HLT_LED,
  output RA_LED15,
  output RA_LED14,
  output RA_LED13,
  output RA_LED12,
  output RA_LED11,
  output RA_LED10,
  output RA_LED9,
  output RA_LED8,
  output RA_LED7,
  output RA_LED6,
  output RA_LED5,
  output RA_LED4,
  output RA_LED3,
  output RA_LED2,
  output RA_LED1,
  output RA_LED0,
  output MAR_LED11,
  output MAR_LED10,
  output MAR_LED9,
  output MAR_LED8,
  output MAR_LED7,
  output MAR_LED6,
  output MAR_LED5,
  output MAR_LED4,
  output MAR_LED3,
  output MAR_LED2,
  output MAR_LED1,
  output MAR_LED0,
  output MAR_ProgLED,
  output MAR_RunLED,
  output ALU_OVR_LED,
  output ALU_CF_LED,
  output ALU_ZF_LED,
  output ALU_LED15,
  output ALU_LED14,
  output ALU_LED13,
  output ALU_LED12,
  output ALU_LED11,
  output ALU_LED10,
  output ALU_LED9,
  output ALU_LED8,
  output ALU_LED7,
  output ALU_LED6,
  output ALU_LED5,
  output ALU_LED4,
  output ALU_LED3,
  output ALU_LED2,
  output ALU_LED1,
  output ALU_LED0,
  output RAM_LED15,
  output RAM_LED14,
  output RAM_LED13,
  output RAM_LED12,
  output RAM_LED11,
  output RAM_LED10,
  output RAM_LED9,
  output RAM_LED8,
  output RAM_LED7,
  output RAM_LED6,
  output RAM_LED5,
  output RAM_LED4,
  output RAM_LED3,
  output RAM_LED2,
  output RAM_LED1,
  output RAM_LED0,
  output IR_LED15,
  output IR_LED14,
  output IR_LED13,
  output IR_LED12,
  output IR_LED11,
  output IR_LED10,
  output IR_LED9,
  output IR_LED8,
  output IR_LED7,
  output IR_LED6,
  output IR_LED5,
  output IR_LED4,
  output IR_LED3,
  output IR_LED2,
  output IR_LED1,
  output IR_LED0,
  output RB_LED15,
  output RB_LED14,
  output RB_LED13,
  output RB_LED12,
  output RB_LED11,
  output RB_LED10,
  output RB_LED9,
  output RB_LED8,
  output RB_LED7,
  output RB_LED6,
  output RB_LED5,
  output RB_LED4,
  output RB_LED3,
  output RB_LED2,
  output RB_LED1,
  output RB_LED0,
  output OUT_Seg3_A,
  output OUT_Seg2_A,
  output OUT_Seg3_B,
  output OUT_Seg1_A,
  output OUT_Seg2_B,
  output OUT_Seg3_C,
  output OUT_Seg0_A,
  output OUT_Seg1_B,
  output OUT_Seg2_C,
  output OUT_Seg3_D,
  output OUT_Seg0_B,
  output OUT_Seg1_C,
  output OUT_Seg2_D,
  output OUT_Seg3_E,
  output OUT_Seg0_C,
  output OUT_Seg1_D,
  output OUT_Seg2_E,
  output OUT_Seg3_F,
  output OUT_Seg0_D,
  output OUT_Seg1_E,
  output OUT_Seg2_F,
  output OUT_Seg3_G,
  output OUT_Seg0_E,
  output OUT_Seg1_F,
  output OUT_Seg2_G,
  output BUS_LED15,
  output BUS_LED14,
  output BUS_LED13,
  output BUS_LED12,
  output BUS_LED11,
  output BUS_LED10,
  output BUS_LED9,
  output BUS_LED8,
  output BUS_LED7,
  output BUS_LED6,
  output BUS_LED5,
  output BUS_LED4,
  output BUS_LED3,
  output BUS_LED2,
  output BUS_LED1,
  output BUS_LED0,
  output OUT_Seg0_F,
  output OUT_Seg1_G,
  output OUT_Seg0_G,
  output CTRL_NT_LED,
  output CTRL_AN_LED,
  output CTRL_OR_LED,
  output CTRL_XR_LED,
  output CTRL_FI_LED,
  output CTRL_J_LED,
  output CTRL_CO_LED,
  output CTRL_CE_LED,
  output CTRL_OI_LED,
  output CTRL_BI_LED,
  output CTRL_SU_LED,
  output CTRL_EO_LED,
  output CTRL_AO_LED,
  output CTRL_AI_LED,
  output CTRL_II_LED,
  output CTRL_IO_LED,
  output CTRL_RO_LED,
  output CTRL_RI_LED,
  output CTRL_MI_LED,
  output CTRL_HLT_LED,
  output CTRL_TimeLED0,
  output CTRL_TimeLED2,
  output CTRL_TimeLED4,
  output CTRL_CountLED2,
  output CTRL_CountLED1,
  output CTRL_CountLED0,
  output CTRL_TimeLED1,
  output CTRL_TimeLED3
);

  wire partmar_1_prog;
  wire [3:0] partir_1_rego;
  wire [11:0] partmar_1_a;
  wire [15:0] partreg_1_rego, partreg_2_rego;
  wire [25:1] partctrl_1_mi_1a8064a7;

  partCLK partclk_1 (
    .CLK(partctrl_1_mi_1a8064a7[24]), .Mode(CLK_Mode), .HLT(CLK_HLT_LED), .Pulse(CLK_Pulse),
    .CLK_7d3332a1(partctrl_1_mi_1a8064a7[25]), .LED(CLK_LED));
  partMAR partmar_1 (
    .RunLED(MAR_RunLED),
    .AddrSWs_d391c16e({MAR_AddrSW11, MAR_AddrSW10, MAR_AddrSW9, MAR_AddrSW8, MAR_AddrSW7, MAR_AddrSW6, MAR_AddrSW5, MAR_AddrSW4, MAR_AddrSW3, MAR_AddrSW2, MAR_AddrSW1, MAR_AddrSW0}),
    .A_LEDs({MAR_LED11, MAR_LED10, MAR_LED9, MAR_LED8, MAR_LED7, MAR_LED6, MAR_LED5, MAR_LED4, MAR_LED3, MAR_LED2, MAR_LED1, MAR_LED0}),
    .CLR(partctrl_1_mi_1a8064a7[22]), .Mode(MAR_Mode), .CLK(partctrl_1_mi_1a8064a7[24]),
    .BusI({BUS_LED11, BUS_LED10, BUS_LED9, BUS_LED8, BUS_LED7, BUS_LED6, BUS_LED5, BUS_LED4, BUS_LED3, BUS_LED2, BUS_LED1, BUS_LED0}),
    .MI_85f63c41(partctrl_1_mi_1a8064a7[1]), .A(partmar_1_a), .ProgLED(MAR_ProgLED), .PROG(partmar_1_prog));
  partRAM partram_1 (
    .ProgOK(RAM_ProgOK),
    .LEDs({RAM_LED15, RAM_LED14, RAM_LED13, RAM_LED12, RAM_LED11, RAM_LED10, RAM_LED9, RAM_LED8, RAM_LED7, RAM_LED6, RAM_LED5, RAM_LED4, RAM_LED3, RAM_LED2, RAM_LED1, RAM_LED0}),
    .RI(partctrl_1_mi_1a8064a7[2]), .A(partmar_1_a),
    .ProgSW({RAM_ProgSW15, RAM_ProgSW14, RAM_ProgSW13, RAM_ProgSW12, RAM_ProgSW11, RAM_ProgSW10, RAM_ProgSW9, RAM_ProgSW8, RAM_ProgSW7, RAM_ProgSW6, RAM_ProgSW5, RAM_ProgSW4, RAM_ProgSW3, RAM_ProgSW2, RAM_ProgSW1, RAM_ProgSW0}),
    .BusI({BUS_LED15, BUS_LED14, BUS_LED13, BUS_LED12, BUS_LED11, BUS_LED10, BUS_LED9, BUS_LED8, BUS_LED7, BUS_LED6, BUS_LED5, BUS_LED4, BUS_LED3, BUS_LED2, BUS_LED1, BUS_LED0}),
    .CLK(partctrl_1_mi_1a8064a7[24]), .RO_b3172779(partctrl_1_mi_1a8064a7[3]), .PROG(partmar_1_prog),
    .BusO({BUS_LED15, BUS_LED14, BUS_LED13, BUS_LED12, BUS_LED11, BUS_LED10, BUS_LED9, BUS_LED8, BUS_LED7, BUS_LED6, BUS_LED5, BUS_LED4, BUS_LED3, BUS_LED2, BUS_LED1, BUS_LED0}),
    .CLR(RAM_Clear));
  Pull_Resistor pull_resistor_1 (.node({BUS_LED15, BUS_LED14, BUS_LED13, BUS_LED12, BUS_LED11, BUS_LED10, BUS_LED9, BUS_LED8, BUS_LED7, BUS_LED6, BUS_LED5, BUS_LED4, BUS_LED3, BUS_LED2, BUS_LED1, BUS_LED0}));
  partIR partir_1 (
    .LEDs({IR_LED15, IR_LED14, IR_LED13, IR_LED12, IR_LED11, IR_LED10, IR_LED9, IR_LED8, IR_LED7, IR_LED6, IR_LED5, IR_LED4, IR_LED3, IR_LED2, IR_LED1, IR_LED0}),
    .BusI({BUS_LED15, BUS_LED14, BUS_LED13, BUS_LED12, BUS_LED11, BUS_LED10, BUS_LED9, BUS_LED8, BUS_LED7, BUS_LED6, BUS_LED5, BUS_LED4, BUS_LED3, BUS_LED2, BUS_LED1, BUS_LED0}),
    .CLK(partctrl_1_mi_1a8064a7[24]), .IO_a1d15099(partctrl_1_mi_1a8064a7[4]),
    .CLR(partctrl_1_mi_1a8064a7[22]), .II_193c5152(partctrl_1_mi_1a8064a7[5]),
    .BusO({BUS_LED15, BUS_LED14, BUS_LED13, BUS_LED12, BUS_LED11, BUS_LED10, BUS_LED9, BUS_LED8, BUS_LED7, BUS_LED6, BUS_LED5, BUS_LED4, BUS_LED3, BUS_LED2, BUS_LED1, BUS_LED0}),
    .RegO(partir_1_rego));
  partCTRL partctrl_1 (
    .CLR(partctrl_1_mi_1a8064a7[22]), .MI_1a8064a7(partctrl_1_mi_1a8064a7[1]),
    .CFI(partctrl_1_mi_1a8064a7[20]), .AI_f325b2de(partctrl_1_mi_1a8064a7[6]),
    .J_e6dac3f4(partctrl_1_mi_1a8064a7[14]), .CLR_87b95d37(partctrl_1_mi_1a8064a7[23]),
    .II_51e65cc3(partctrl_1_mi_1a8064a7[5]), .RegI(partir_1_rego), .RI(partctrl_1_mi_1a8064a7[2]),
    .CE(partctrl_1_mi_1a8064a7[12]), .HLT(CLK_HLT_LED), .ZFI(partctrl_1_mi_1a8064a7[21]),
    .AO_fda11864(partctrl_1_mi_1a8064a7[7]), .FI_fa84cb50(partctrl_1_mi_1a8064a7[15]),
    .Time_LEDs_backwards({CTRL_TimeLED0, CTRL_TimeLED1, CTRL_TimeLED2, CTRL_TimeLED3, CTRL_TimeLED4}),
    .IO_06df68e4(partctrl_1_mi_1a8064a7[4]), .CLK_0416f44f(partctrl_1_mi_1a8064a7[25]),
    .RO_f7a11c4b(partctrl_1_mi_1a8064a7[3]), .CO_e8fa446c(partctrl_1_mi_1a8064a7[13]),
    .Count_LEDs({CTRL_CountLED2, CTRL_CountLED1, CTRL_CountLED0}), .Reset(MasterReset),
    .OI(partctrl_1_mi_1a8064a7[11]), .BI_dc5a9e0c(partctrl_1_mi_1a8064a7[10]),
    .SU(partctrl_1_mi_1a8064a7[9]), .EO_bf3b4110(partctrl_1_mi_1a8064a7[8]), .NT(partctrl_1_mi_1a8064a7[19]),
    .AN(partctrl_1_mi_1a8064a7[18]), .R(partctrl_1_mi_1a8064a7[17]), .XR(partctrl_1_mi_1a8064a7[16]),
    .CTRL_LEDs({CTRL_NT_LED, CTRL_AN_LED, CTRL_OR_LED, CTRL_XR_LED, CTRL_FI_LED, CTRL_J_LED, CTRL_CO_LED, CTRL_CE_LED, CTRL_OI_LED, CTRL_BI_LED, CTRL_SU_LED, CTRL_EO_LED, CTRL_AO_LED, CTRL_AI_LED, CTRL_II_LED, CTRL_IO_LED, CTRL_RO_LED, CTRL_RI_LED, CTRL_MI_LED, CTRL_HLT_LED}));
  Pull_Resistor pull_resistor_2 (.node({partctrl_1_mi_1a8064a7, CLK_HLT_LED}));
  partREG partreg_1 (
    .RegO(partreg_1_rego), .CLK(partctrl_1_mi_1a8064a7[24]), .CLR(partctrl_1_mi_1a8064a7[22]),
    .BusO({BUS_LED15, BUS_LED14, BUS_LED13, BUS_LED12, BUS_LED11, BUS_LED10, BUS_LED9, BUS_LED8, BUS_LED7, BUS_LED6, BUS_LED5, BUS_LED4, BUS_LED3, BUS_LED2, BUS_LED1, BUS_LED0}),
    .xI_9c528b91(partctrl_1_mi_1a8064a7[6]), .xO_05de6390(partctrl_1_mi_1a8064a7[7]),
    .BusI({BUS_LED15, BUS_LED14, BUS_LED13, BUS_LED12, BUS_LED11, BUS_LED10, BUS_LED9, BUS_LED8, BUS_LED7, BUS_LED6, BUS_LED5, BUS_LED4, BUS_LED3, BUS_LED2, BUS_LED1, BUS_LED0}),
    .LEDs({RA_LED15, RA_LED14, RA_LED13, RA_LED12, RA_LED11, RA_LED10, RA_LED9, RA_LED8, RA_LED7, RA_LED6, RA_LED5, RA_LED4, RA_LED3, RA_LED2, RA_LED1, RA_LED0}));
  partALU partalu_1 (
    .BusO({BUS_LED15, BUS_LED14, BUS_LED13, BUS_LED12, BUS_LED11, BUS_LED10, BUS_LED9, BUS_LED8, BUS_LED7, BUS_LED6, BUS_LED5, BUS_LED4, BUS_LED3, BUS_LED2, BUS_LED1, BUS_LED0}),
    .A(partreg_1_rego), .EO_a0c37f53(partctrl_1_mi_1a8064a7[8]), .NT(partctrl_1_mi_1a8064a7[19]),
    .RES_LEDs({ALU_LED15, ALU_LED14, ALU_LED13, ALU_LED12, ALU_LED11, ALU_LED10, ALU_LED9, ALU_LED8, ALU_LED7, ALU_LED6, ALU_LED5, ALU_LED4, ALU_LED3, ALU_LED2, ALU_LED1, ALU_LED0}),
    .B(partreg_2_rego), .SU(partctrl_1_mi_1a8064a7[9]), .AN(partctrl_1_mi_1a8064a7[18]),
    .CLK(partctrl_1_mi_1a8064a7[24]), .CLR(partctrl_1_mi_1a8064a7[22]), .XR(partctrl_1_mi_1a8064a7[16]),
    .R(partctrl_1_mi_1a8064a7[17]), .FI_261165dc(partctrl_1_mi_1a8064a7[15]), .Overflow(ALU_OVR_LED),
    .CF_LED(ALU_CF_LED), .ZF_LED(ALU_ZF_LED), .CF(partctrl_1_mi_1a8064a7[20]), .ZF(partctrl_1_mi_1a8064a7[21]));
  partREG partreg_2 (
    .RegO(partreg_2_rego), .CLK(partctrl_1_mi_1a8064a7[24]), .CLR(partctrl_1_mi_1a8064a7[22]),
    .BusO({BUS_LED15, BUS_LED14, BUS_LED13, BUS_LED12, BUS_LED11, BUS_LED10, BUS_LED9, BUS_LED8, BUS_LED7, BUS_LED6, BUS_LED5, BUS_LED4, BUS_LED3, BUS_LED2, BUS_LED1, BUS_LED0}),
    .xI_9c528b91(partctrl_1_mi_1a8064a7[10]), .xO_05de6390(1'b1),
    .BusI({BUS_LED15, BUS_LED14, BUS_LED13, BUS_LED12, BUS_LED11, BUS_LED10, BUS_LED9, BUS_LED8, BUS_LED7, BUS_LED6, BUS_LED5, BUS_LED4, BUS_LED3, BUS_LED2, BUS_LED1, BUS_LED0}),
    .LEDs({RB_LED15, RB_LED14, RB_LED13, RB_LED12, RB_LED11, RB_LED10, RB_LED9, RB_LED8, RB_LED7, RB_LED6, RB_LED5, RB_LED4, RB_LED3, RB_LED2, RB_LED1, RB_LED0}));
  partOUT partout_1 (
    .Hex(OUT_Hex), .OI(partctrl_1_mi_1a8064a7[11]), .Twos(OUT_Twos),
    .SSeg2({OUT_Seg2_G, OUT_Seg2_F, OUT_Seg2_E, OUT_Seg2_D, OUT_Seg2_C, OUT_Seg2_B, OUT_Seg2_A}),
    .BusI({BUS_LED15, BUS_LED14, BUS_LED13, BUS_LED12, BUS_LED11, BUS_LED10, BUS_LED9, BUS_LED8, BUS_LED7, BUS_LED6, BUS_LED5, BUS_LED4, BUS_LED3, BUS_LED2, BUS_LED1, BUS_LED0}),
    .CLR_898658ba(partctrl_1_mi_1a8064a7[23]), .CLK(partctrl_1_mi_1a8064a7[24]),
    .SSeg3({OUT_Seg3_G, OUT_Seg3_F, OUT_Seg3_E, OUT_Seg3_D, OUT_Seg3_C, OUT_Seg3_B, OUT_Seg3_A}),
    .SSeg1({OUT_Seg1_G, OUT_Seg1_F, OUT_Seg1_E, OUT_Seg1_D, OUT_Seg1_C, OUT_Seg1_B, OUT_Seg1_A}),
    .SSeg0({OUT_Seg0_G, OUT_Seg0_F, OUT_Seg0_E, OUT_Seg0_D, OUT_Seg0_C, OUT_Seg0_B, OUT_Seg0_A}));
  partPC partpc_1 (
    .BusO({BUS_LED11, BUS_LED10, BUS_LED9, BUS_LED8, BUS_LED7, BUS_LED6, BUS_LED5, BUS_LED4, BUS_LED3, BUS_LED2, BUS_LED1, BUS_LED0}),
    .CLK(partctrl_1_mi_1a8064a7[24]), .CLR_b6b4cc54(partctrl_1_mi_1a8064a7[23]),
    .CE(partctrl_1_mi_1a8064a7[12]),
    .BusI({BUS_LED11, BUS_LED10, BUS_LED9, BUS_LED8, BUS_LED7, BUS_LED6, BUS_LED5, BUS_LED4, BUS_LED3, BUS_LED2, BUS_LED1, BUS_LED0}),
    .CO_d457f91e(partctrl_1_mi_1a8064a7[13]), .J_ab0d5ac6(partctrl_1_mi_1a8064a7[14]),
    .LEDs({PC_LED11, PC_LED10, PC_LED9, PC_LED8, PC_LED7, PC_LED6, PC_LED5, PC_LED4, PC_LED3, PC_LED2, PC_LED1, PC_LED0}));  // open: TerminalCount

  assign PWR_LED = PWR;
endmodule

module mainExternal (
  input  Power,
  input  Mode,
  input  Mode_2,
  input  Hex,
  input  Sign,
  input  in_6,
  input  in_7,
  input  in_8,
  input  in_9,
  input  Memory,
  input  in_11,
  input  in_12,
  input  Address,
  input  in_14,
  input  in_15,
  input  in_16,
  input  in_17,
  input  in_18,
  input  in_19,
  input  in_20,
  input  in_21,
  input  in_22,
  input  in_23,
  input  RAM,
  input  in_25,
  input  in_26,
  input  Contents,
  input  in_28,
  input  in_29,
  input  in_30,
  input  in_31,
  input  in_32,
  input  in_33
);

  wire Accept_out, Clear_out, maininternal_1_alu_cf_led, maininternal_1_alu_led0, maininternal_1_alu_led1,
       maininternal_1_alu_led2, maininternal_1_alu_led3, maininternal_1_alu_led4, maininternal_1_alu_led5,
       maininternal_1_alu_led6, maininternal_1_alu_led7, maininternal_1_alu_led8, maininternal_1_alu_led9,
       maininternal_1_alu_led10, maininternal_1_alu_led11, maininternal_1_alu_led12,
       maininternal_1_alu_led13, maininternal_1_alu_led14, maininternal_1_alu_led15,
       maininternal_1_alu_ovr_led, maininternal_1_alu_zf_led, maininternal_1_bus_led0,
       maininternal_1_bus_led1, maininternal_1_bus_led2, maininternal_1_bus_led3, maininternal_1_bus_led4,
       maininternal_1_bus_led5, maininternal_1_bus_led6, maininternal_1_bus_led7, maininternal_1_bus_led8,
       maininternal_1_bus_led9, maininternal_1_bus_led10, maininternal_1_bus_led11, maininternal_1_bus_led12,
       maininternal_1_bus_led13, maininternal_1_bus_led14, maininternal_1_bus_led15,
       maininternal_1_clk_hlt_led, maininternal_1_clk_led, maininternal_1_ctrl_ai_led,
       maininternal_1_ctrl_an_led, maininternal_1_ctrl_ao_led, maininternal_1_ctrl_bi_led,
       maininternal_1_ctrl_ce_led, maininternal_1_ctrl_co_led, maininternal_1_ctrl_countled0,
       maininternal_1_ctrl_countled1, maininternal_1_ctrl_countled2, maininternal_1_ctrl_eo_led,
       maininternal_1_ctrl_fi_led, maininternal_1_ctrl_hlt_led, maininternal_1_ctrl_ii_led,
       maininternal_1_ctrl_io_led, maininternal_1_ctrl_j_led, maininternal_1_ctrl_mi_led,
       maininternal_1_ctrl_nt_led, maininternal_1_ctrl_oi_led, maininternal_1_ctrl_or_led,
       maininternal_1_ctrl_ri_led, maininternal_1_ctrl_ro_led, maininternal_1_ctrl_su_led,
       maininternal_1_ctrl_timeled0, maininternal_1_ctrl_timeled1, maininternal_1_ctrl_timeled2,
       maininternal_1_ctrl_timeled3, maininternal_1_ctrl_timeled4, maininternal_1_ctrl_xr_led,
       maininternal_1_ir_led0, maininternal_1_ir_led1, maininternal_1_ir_led2, maininternal_1_ir_led3,
       maininternal_1_ir_led4, maininternal_1_ir_led5, maininternal_1_ir_led6, maininternal_1_ir_led7,
       maininternal_1_ir_led8, maininternal_1_ir_led9, maininternal_1_ir_led10, maininternal_1_ir_led11,
       maininternal_1_ir_led12, maininternal_1_ir_led13, maininternal_1_ir_led14, maininternal_1_ir_led15,
       maininternal_1_mar_led0, maininternal_1_mar_led1, maininternal_1_mar_led2, maininternal_1_mar_led3,
       maininternal_1_mar_led4, maininternal_1_mar_led5, maininternal_1_mar_led6, maininternal_1_mar_led7,
       maininternal_1_mar_led8, maininternal_1_mar_led9, maininternal_1_mar_led10, maininternal_1_mar_led11,
       maininternal_1_mar_progled, maininternal_1_mar_runled, maininternal_1_out_seg0_a,
       maininternal_1_out_seg0_b, maininternal_1_out_seg0_c, maininternal_1_out_seg0_d,
       maininternal_1_out_seg0_e, maininternal_1_out_seg0_f, maininternal_1_out_seg0_g,
       maininternal_1_out_seg1_a, maininternal_1_out_seg1_b, maininternal_1_out_seg1_c,
       maininternal_1_out_seg1_d, maininternal_1_out_seg1_e, maininternal_1_out_seg1_f,
       maininternal_1_out_seg1_g, maininternal_1_out_seg2_a, maininternal_1_out_seg2_b,
       maininternal_1_out_seg2_c, maininternal_1_out_seg2_d, maininternal_1_out_seg2_e,
       maininternal_1_out_seg2_f, maininternal_1_out_seg2_g, maininternal_1_out_seg3_a,
       maininternal_1_out_seg3_b, maininternal_1_out_seg3_c, maininternal_1_out_seg3_d,
       maininternal_1_out_seg3_e, maininternal_1_out_seg3_f, maininternal_1_out_seg3_g,
       maininternal_1_pc_led0, maininternal_1_pc_led1, maininternal_1_pc_led2, maininternal_1_pc_led3,
       maininternal_1_pc_led4, maininternal_1_pc_led5, maininternal_1_pc_led6, maininternal_1_pc_led7,
       maininternal_1_pc_led8, maininternal_1_pc_led9, maininternal_1_pc_led10, maininternal_1_pc_led11,
       maininternal_1_pwr_led, maininternal_1_ra_led0, maininternal_1_ra_led1, maininternal_1_ra_led2,
       maininternal_1_ra_led3, maininternal_1_ra_led4, maininternal_1_ra_led5, maininternal_1_ra_led6,
       maininternal_1_ra_led7, maininternal_1_ra_led8, maininternal_1_ra_led9, maininternal_1_ra_led10,
       maininternal_1_ra_led11, maininternal_1_ra_led12, maininternal_1_ra_led13, maininternal_1_ra_led14,
       maininternal_1_ra_led15, maininternal_1_ram_led0, maininternal_1_ram_led1, maininternal_1_ram_led2,
       maininternal_1_ram_led3, maininternal_1_ram_led4, maininternal_1_ram_led5, maininternal_1_ram_led6,
       maininternal_1_ram_led7, maininternal_1_ram_led8, maininternal_1_ram_led9, maininternal_1_ram_led10,
       maininternal_1_ram_led11, maininternal_1_ram_led12, maininternal_1_ram_led13,
       maininternal_1_ram_led14, maininternal_1_ram_led15, maininternal_1_rb_led0, maininternal_1_rb_led1,
       maininternal_1_rb_led2, maininternal_1_rb_led3, maininternal_1_rb_led4, maininternal_1_rb_led5,
       maininternal_1_rb_led6, maininternal_1_rb_led7, maininternal_1_rb_led8, maininternal_1_rb_led9,
       maininternal_1_rb_led10, maininternal_1_rb_led11, maininternal_1_rb_led12, maininternal_1_rb_led13,
       maininternal_1_rb_led14, maininternal_1_rb_led15, Pulse_out, Reset_out;

  LED Live (.in(maininternal_1_pwr_led));
  mainInternal maininternal_1 (
    .RB_LED3(maininternal_1_rb_led3), .RB_LED0(maininternal_1_rb_led0), .RB_LED2(maininternal_1_rb_led2),
    .RB_LED1(maininternal_1_rb_led1), .RB_LED4(maininternal_1_rb_led4), .RB_LED5(maininternal_1_rb_led5),
    .RB_LED6(maininternal_1_rb_led6), .RB_LED7(maininternal_1_rb_led7), .RB_LED8(maininternal_1_rb_led8),
    .RB_LED9(maininternal_1_rb_led9), .RB_LED10(maininternal_1_rb_led10), .RB_LED11(maininternal_1_rb_led11),
    .RB_LED12(maininternal_1_rb_led12), .RB_LED13(maininternal_1_rb_led13),
    .RB_LED14(maininternal_1_rb_led14), .RB_LED15(maininternal_1_rb_led15), .IR_LED0(maininternal_1_ir_led0),
    .IR_LED1(maininternal_1_ir_led1), .IR_LED2(maininternal_1_ir_led2), .IR_LED3(maininternal_1_ir_led3),
    .IR_LED4(maininternal_1_ir_led4), .IR_LED5(maininternal_1_ir_led5), .IR_LED6(maininternal_1_ir_led6),
    .IR_LED7(maininternal_1_ir_led7), .IR_LED8(maininternal_1_ir_led8), .IR_LED9(maininternal_1_ir_led9),
    .IR_LED10(maininternal_1_ir_led10), .IR_LED11(maininternal_1_ir_led11),
    .IR_LED12(maininternal_1_ir_led12), .IR_LED13(maininternal_1_ir_led13),
    .IR_LED14(maininternal_1_ir_led14), .IR_LED15(maininternal_1_ir_led15),
    .RAM_LED0(maininternal_1_ram_led0), .RAM_LED1(maininternal_1_ram_led1),
    .RAM_LED2(maininternal_1_ram_led2), .RAM_LED3(maininternal_1_ram_led3),
    .RAM_LED4(maininternal_1_ram_led4), .RAM_LED5(maininternal_1_ram_led5),
    .RAM_LED6(maininternal_1_ram_led6), .RAM_LED7(maininternal_1_ram_led7),
    .RAM_LED8(maininternal_1_ram_led8), .RAM_LED9(maininternal_1_ram_led9),
    .RAM_LED10(maininternal_1_ram_led10), .RAM_LED11(maininternal_1_ram_led11),
    .RAM_LED12(maininternal_1_ram_led12), .RAM_LED13(maininternal_1_ram_led13),
    .RAM_LED14(maininternal_1_ram_led14), .RAM_LED15(maininternal_1_ram_led15),
    .ALU_LED0(maininternal_1_alu_led0), .ALU_LED1(maininternal_1_alu_led1),
    .ALU_LED2(maininternal_1_alu_led2), .ALU_LED3(maininternal_1_alu_led3),
    .ALU_LED4(maininternal_1_alu_led4), .ALU_LED5(maininternal_1_alu_led5),
    .ALU_LED6(maininternal_1_alu_led6), .ALU_LED7(maininternal_1_alu_led7),
    .ALU_LED8(maininternal_1_alu_led8), .ALU_LED9(maininternal_1_alu_led9),
    .ALU_LED10(maininternal_1_alu_led10), .ALU_LED11(maininternal_1_alu_led11),
    .ALU_LED12(maininternal_1_alu_led12), .ALU_LED13(maininternal_1_alu_led13),
    .ALU_LED14(maininternal_1_alu_led14), .ALU_LED15(maininternal_1_alu_led15),
    .ALU_ZF_LED(maininternal_1_alu_zf_led), .ALU_CF_LED(maininternal_1_alu_cf_led),
    .ALU_OVR_LED(maininternal_1_alu_ovr_led), .MAR_RunLED(maininternal_1_mar_runled),
    .MAR_ProgLED(maininternal_1_mar_progled), .MAR_LED0(maininternal_1_mar_led0),
    .MAR_LED1(maininternal_1_mar_led1), .MAR_LED2(maininternal_1_mar_led2),
    .MAR_LED3(maininternal_1_mar_led3), .MAR_LED4(maininternal_1_mar_led4),
    .MAR_LED5(maininternal_1_mar_led5), .MAR_LED6(maininternal_1_mar_led6),
    .MAR_LED7(maininternal_1_mar_led7), .MAR_LED8(maininternal_1_mar_led8),
    .MAR_LED9(maininternal_1_mar_led9), .MAR_LED10(maininternal_1_mar_led10),
    .MAR_LED11(maininternal_1_mar_led11), .RA_LED0(maininternal_1_ra_led0), .RA_LED1(maininternal_1_ra_led1),
    .RA_LED2(maininternal_1_ra_led2), .RA_LED3(maininternal_1_ra_led3), .RA_LED4(maininternal_1_ra_led4),
    .RA_LED5(maininternal_1_ra_led5), .RA_LED6(maininternal_1_ra_led6), .RA_LED7(maininternal_1_ra_led7),
    .RA_LED8(maininternal_1_ra_led8), .RA_LED9(maininternal_1_ra_led9), .RA_LED10(maininternal_1_ra_led10),
    .RA_LED11(maininternal_1_ra_led11), .RA_LED12(maininternal_1_ra_led12),
    .RA_LED13(maininternal_1_ra_led13), .RA_LED14(maininternal_1_ra_led14),
    .RA_LED15(maininternal_1_ra_led15), .CLK_HLT_LED(maininternal_1_clk_hlt_led),
    .PC_LED0(maininternal_1_pc_led0), .PC_LED1(maininternal_1_pc_led1), .PC_LED2(maininternal_1_pc_led2),
    .PC_LED3(maininternal_1_pc_led3), .PC_LED4(maininternal_1_pc_led4), .PC_LED5(maininternal_1_pc_led5),
    .PC_LED6(maininternal_1_pc_led6), .PC_LED7(maininternal_1_pc_led7), .PC_LED8(maininternal_1_pc_led8),
    .PC_LED9(maininternal_1_pc_led9), .PC_LED10(maininternal_1_pc_led10), .PC_LED11(maininternal_1_pc_led11),
    .CLK_LED(maininternal_1_clk_led), .PWR_LED(maininternal_1_pwr_led), .MasterReset(Reset_out),
    .OUT_Twos(Sign), .OUT_Hex(Hex), .RAM_ProgSW0(in_33), .RAM_ProgSW1(in_32), .RAM_ProgSW2(in_31),
    .RAM_ProgSW3(in_30), .RAM_ProgSW4(in_29), .RAM_ProgSW5(in_28), .RAM_ProgSW6(Contents),
    .RAM_ProgSW7(in_26), .RAM_ProgSW8(in_25), .RAM_ProgSW9(RAM), .RAM_ProgSW10(in_23), .RAM_ProgSW11(in_22),
    .RAM_ProgSW12(in_21), .RAM_ProgSW13(in_20), .RAM_ProgSW14(in_19), .RAM_ProgSW15(in_18),
    .RAM_ProgOK(Accept_out), .RAM_Clear(Clear_out), .MAR_Mode(Mode_2), .MAR_AddrSW0(in_17),
    .MAR_AddrSW1(in_16), .MAR_AddrSW2(in_15), .MAR_AddrSW3(in_14), .MAR_AddrSW4(Address),
    .MAR_AddrSW5(in_12), .MAR_AddrSW6(in_11), .MAR_AddrSW7(Memory), .MAR_AddrSW8(in_9), .MAR_AddrSW9(in_8),
    .MAR_AddrSW10(in_7), .MAR_AddrSW11(in_6), .CLK_Mode(Mode), .CLK_Pulse(Pulse_out), .PWR(Power),
    .OUT_Seg3_A(maininternal_1_out_seg3_a), .OUT_Seg2_A(maininternal_1_out_seg2_a),
    .OUT_Seg3_B(maininternal_1_out_seg3_b), .OUT_Seg1_A(maininternal_1_out_seg1_a),
    .OUT_Seg2_B(maininternal_1_out_seg2_b), .OUT_Seg3_C(maininternal_1_out_seg3_c),
    .OUT_Seg0_A(maininternal_1_out_seg0_a), .OUT_Seg1_B(maininternal_1_out_seg1_b),
    .OUT_Seg2_C(maininternal_1_out_seg2_c), .OUT_Seg3_D(maininternal_1_out_seg3_d),
    .OUT_Seg0_B(maininternal_1_out_seg0_b), .OUT_Seg1_C(maininternal_1_out_seg1_c),
    .OUT_Seg2_D(maininternal_1_out_seg2_d), .OUT_Seg3_E(maininternal_1_out_seg3_e),
    .OUT_Seg0_C(maininternal_1_out_seg0_c), .OUT_Seg1_D(maininternal_1_out_seg1_d),
    .OUT_Seg2_E(maininternal_1_out_seg2_e), .OUT_Seg3_F(maininternal_1_out_seg3_f),
    .OUT_Seg0_D(maininternal_1_out_seg0_d), .OUT_Seg1_E(maininternal_1_out_seg1_e),
    .OUT_Seg2_F(maininternal_1_out_seg2_f), .OUT_Seg3_G(maininternal_1_out_seg3_g),
    .OUT_Seg0_E(maininternal_1_out_seg0_e), .OUT_Seg1_F(maininternal_1_out_seg1_f),
    .OUT_Seg2_G(maininternal_1_out_seg2_g), .BUS_LED15(maininternal_1_bus_led15),
    .BUS_LED14(maininternal_1_bus_led14), .BUS_LED13(maininternal_1_bus_led13),
    .BUS_LED12(maininternal_1_bus_led12), .BUS_LED11(maininternal_1_bus_led11),
    .BUS_LED10(maininternal_1_bus_led10), .BUS_LED9(maininternal_1_bus_led9),
    .BUS_LED8(maininternal_1_bus_led8), .BUS_LED7(maininternal_1_bus_led7),
    .BUS_LED6(maininternal_1_bus_led6), .BUS_LED5(maininternal_1_bus_led5),
    .BUS_LED4(maininternal_1_bus_led4), .BUS_LED3(maininternal_1_bus_led3),
    .BUS_LED2(maininternal_1_bus_led2), .BUS_LED1(maininternal_1_bus_led1),
    .BUS_LED0(maininternal_1_bus_led0), .OUT_Seg0_F(maininternal_1_out_seg0_f),
    .OUT_Seg1_G(maininternal_1_out_seg1_g), .OUT_Seg0_G(maininternal_1_out_seg0_g),
    .CTRL_NT_LED(maininternal_1_ctrl_nt_led), .CTRL_AN_LED(maininternal_1_ctrl_an_led),
    .CTRL_OR_LED(maininternal_1_ctrl_or_led), .CTRL_XR_LED(maininternal_1_ctrl_xr_led),
    .CTRL_FI_LED(maininternal_1_ctrl_fi_led), .CTRL_J_LED(maininternal_1_ctrl_j_led),
    .CTRL_CO_LED(maininternal_1_ctrl_co_led), .CTRL_CE_LED(maininternal_1_ctrl_ce_led),
    .CTRL_OI_LED(maininternal_1_ctrl_oi_led), .CTRL_BI_LED(maininternal_1_ctrl_bi_led),
    .CTRL_SU_LED(maininternal_1_ctrl_su_led), .CTRL_EO_LED(maininternal_1_ctrl_eo_led),
    .CTRL_AO_LED(maininternal_1_ctrl_ao_led), .CTRL_AI_LED(maininternal_1_ctrl_ai_led),
    .CTRL_II_LED(maininternal_1_ctrl_ii_led), .CTRL_IO_LED(maininternal_1_ctrl_io_led),
    .CTRL_RO_LED(maininternal_1_ctrl_ro_led), .CTRL_RI_LED(maininternal_1_ctrl_ri_led),
    .CTRL_MI_LED(maininternal_1_ctrl_mi_led), .CTRL_HLT_LED(maininternal_1_ctrl_hlt_led),
    .CTRL_TimeLED0(maininternal_1_ctrl_timeled0), .CTRL_TimeLED2(maininternal_1_ctrl_timeled2),
    .CTRL_TimeLED4(maininternal_1_ctrl_timeled4), .CTRL_CountLED2(maininternal_1_ctrl_countled2),
    .CTRL_CountLED1(maininternal_1_ctrl_countled1), .CTRL_CountLED0(maininternal_1_ctrl_countled0),
    .CTRL_TimeLED1(maininternal_1_ctrl_timeled1), .CTRL_TimeLED3(maininternal_1_ctrl_timeled3));
  LED led_1 (.in(maininternal_1_bus_led14));
  LED led_2 (.in(maininternal_1_bus_led15));
  LED led_3 (.in(maininternal_1_bus_led13));
  LED led_4 (.in(maininternal_1_ir_led15));
  LED led_5 (.in(maininternal_1_ir_led13));
  LED led_6 (.in(maininternal_1_ir_led14));
  LED led_7 (.in(maininternal_1_ctrl_countled0));
  LED Count (.in(maininternal_1_ctrl_countled1));
  LED led_8 (.in(maininternal_1_ctrl_countled2));
  LED led_9 (.in(maininternal_1_pc_led9));
  LED led_10 (.in(maininternal_1_pc_led10));
  LED led_11 (.in(maininternal_1_pc_led11));
  LED High ();  // open: in
  Button Reset (.out(Reset_out));
  LED led_12 (.in(maininternal_1_bus_led11));
  LED led_13 (.in(maininternal_1_bus_led12));
  LED Current (.in(maininternal_1_bus_led9));
  LED led_14 (.in(maininternal_1_bus_led10));
  LED led_15 (.in(maininternal_1_ir_led10));
  LED Instruction (.in(maininternal_1_ir_led9));
  LED led_16 (.in(maininternal_1_ir_led11));
  LED led_17 (.in(maininternal_1_ir_led12));
  LED Timer (.in(maininternal_1_ctrl_timeled2));
  LED led_18 (.in(maininternal_1_ctrl_timeled3));
  LED led_19 (.in(maininternal_1_ctrl_timeled4));
  LED led_20 (.in(maininternal_1_pc_led5));
  LED led_21 (.in(maininternal_1_pc_led8));
  LED led_22 (.in(maininternal_1_pc_led6));
  LED Prog (.in(maininternal_1_pc_led7));
  Button Speed ();  // open: out
  LED led_23 (.in(maininternal_1_bus_led5));
  LED Value (.in(maininternal_1_bus_led6));
  LED led_24 (.in(maininternal_1_bus_led8));
  LED led_25 (.in(maininternal_1_bus_led7));
  LED led_26 (.in(maininternal_1_ir_led7));
  LED Decoder (.in(maininternal_1_ir_led5));
  LED led_27 (.in(maininternal_1_ir_led8));
  LED led_28 (.in(maininternal_1_ir_led6));
  LED led_29 (.in(maininternal_1_ctrl_timeled0));
  LED led_30 (.in(maininternal_1_ctrl_timeled1));
  LED led_31 (.in(maininternal_1_pc_led3));
  LED led_32 (.in(maininternal_1_pc_led2));
  LED led_33 (.in(maininternal_1_pc_led1));
  LED Counter (.in(maininternal_1_pc_led4));
  Button Pulse (.out(Pulse_out));
  LED led_34 (.in(maininternal_1_bus_led4));
  LED led_35 (.in(maininternal_1_bus_led1));
  LED led_36 (.in(maininternal_1_bus_led3));
  LED led_37 (.in(maininternal_1_bus_led2));
  LED led_38 (.in(maininternal_1_ir_led4));
  LED led_39 (.in(maininternal_1_ir_led3));
  LED led_40 (.in(maininternal_1_ir_led1));
  LED led_41 (.in(maininternal_1_ir_led2));
  LED Carry (.in(maininternal_1_alu_cf_led));
  LED Zero (.in(maininternal_1_alu_zf_led));
  LED led_42 (.in(maininternal_1_ctrl_hlt_led));
  LED led_43 (.in(maininternal_1_ctrl_mi_led));
  LED led_44 (.in(maininternal_1_pc_led0));
  LED Clock (.in(maininternal_1_clk_led));
  LED Halt (.in(maininternal_1_clk_hlt_led));
  LED led_45 (.in(maininternal_1_ra_led15));
  LED led_46 (.in(maininternal_1_ra_led14));
  LED led_47 (.in(maininternal_1_bus_led0));
  LED led_48 (.in(maininternal_1_ir_led0));
  LED led_49 (.in(maininternal_1_alu_led15));
  LED led_50 (.in(maininternal_1_alu_led14));
  LED Over (.in(maininternal_1_alu_ovr_led));
  LED led_51 (.in(maininternal_1_rb_led15));
  LED led_52 (.in(maininternal_1_rb_led14));
  LED led_53 (.in(maininternal_1_ctrl_io_led));
  LED led_54 (.in(maininternal_1_ctrl_ii_led));
  LED led_55 (.in(maininternal_1_ctrl_ri_led));
  LED led_56 (.in(maininternal_1_ctrl_ro_led));
  Button Clear (.out(Clear_out));
  LED led_57 (.in(maininternal_1_ra_led12));
  LED led_58 (.in(maininternal_1_ra_led10));
  LED led_59 (.in(maininternal_1_ra_led13));
  LED led_60 (.in(maininternal_1_ra_led11));
  LED led_61 (.in(maininternal_1_alu_led13));
  LED led_62 (.in(maininternal_1_alu_led12));
  LED led_63 (.in(maininternal_1_alu_led11));
  LED Arithmatic (.in(maininternal_1_alu_led10));
  LED led_64 (.in(maininternal_1_rb_led12));
  LED led_65 (.in(maininternal_1_rb_led13));
  LED led_66 (.in(maininternal_1_rb_led11));
  LED led_67 (.in(maininternal_1_rb_led10));
  LED led_68 (.in(maininternal_1_ctrl_eo_led));
  LED led_69 (.in(maininternal_1_ctrl_su_led));
  LED led_70 (.in(maininternal_1_ctrl_ai_led));
  LED led_71 (.in(maininternal_1_ctrl_ao_led));
  Button Accept (.out(Accept_out));
  LED led_72 (.in(maininternal_1_ra_led7));
  LED led_73 (.in(maininternal_1_ra_led6));
  LED Accumulator (.in(maininternal_1_ra_led8));
  LED led_74 (.in(maininternal_1_ra_led9));
  LED led_75 (.in(maininternal_1_alu_led9));
  LED led_76 (.in(maininternal_1_alu_led6));
  LED led_77 (.in(maininternal_1_alu_led8));
  LED Logic (.in(maininternal_1_alu_led7));
  LED led_78 (.in(maininternal_1_rb_led7));
  LED led_79 (.in(maininternal_1_rb_led9));
  LED General (.in(maininternal_1_rb_led8));
  LED led_80 (.in(maininternal_1_rb_led6));
  LED led_81 (.in(maininternal_1_ctrl_oi_led));
  LED Controls (.in(maininternal_1_ctrl_bi_led));
  LED led_82 (.in(maininternal_1_ctrl_co_led));
  LED led_83 (.in(maininternal_1_ctrl_ce_led));
  LED Program (.in(maininternal_1_mar_progled));
  LED Run (.in(maininternal_1_mar_runled));
  LED led_84 (.in(maininternal_1_ra_led5));
  LED led_85 (.in(maininternal_1_ra_led3));
  LED led_86 (.in(maininternal_1_ra_led2));
  LED led_87 (.in(maininternal_1_ra_led4));
  LED led_88 (.in(maininternal_1_alu_led2));
  LED led_89 (.in(maininternal_1_alu_led3));
  LED led_90 (.in(maininternal_1_alu_led4));
  LED Unit (.in(maininternal_1_alu_led5));
  LED led_91 (.in(maininternal_1_rb_led3));
  LED led_92 (.in(maininternal_1_rb_led2));
  LED led_93 (.in(maininternal_1_rb_led5));
  LED led_94 (.in(maininternal_1_rb_led4));
  LED led_95 (.in(maininternal_1_ctrl_fi_led));
  LED led_96 (.in(maininternal_1_ctrl_xr_led));
  LED led_97 (.in(maininternal_1_ctrl_or_led));
  LED led_98 (.in(maininternal_1_ctrl_j_led));
  LED led_99 (.in(maininternal_1_ra_led1));
  LED led_100 (.in(maininternal_1_ra_led0));
  LED led_101 (.in(maininternal_1_ram_led15));
  LED led_102 (.in(maininternal_1_alu_led0));
  LED led_103 (.in(maininternal_1_alu_led1));
  LED led_104 (.in(maininternal_1_rb_led1));
  LED led_105 (.in(maininternal_1_rb_led0));
  LED led_106 (.in(maininternal_1_ctrl_an_led));
  LED led_107 (.in(maininternal_1_ctrl_nt_led));
  LED led_108 (.in(maininternal_1_mar_led11));
  LED led_109 (.in(maininternal_1_ram_led14));
  LED led_110 (.in(maininternal_1_ram_led13));
  LED led_111 (.in(maininternal_1_ram_led11));
  LED led_112 (.in(maininternal_1_ram_led12));
  _7_Segment_Display u_7_segment_display_1 ();  // open: g, f, a, b, e, d, c, dp
  _7_Segment_Display u_7_segment_display_2 ();  // open: g, f, a, b, e, d, c, dp
  LED led_113 (.in(maininternal_1_mar_led9));
  LED led_114 (.in(maininternal_1_mar_led7));
  LED led_115 (.in(maininternal_1_mar_led8));
  LED led_116 (.in(maininternal_1_mar_led10));
  LED led_117 (.in(maininternal_1_ram_led9));
  LED led_118 (.in(maininternal_1_ram_led8));
  LED led_119 (.in(maininternal_1_ram_led7));
  LED led_120 (.in(maininternal_1_ram_led10));
  _7_Segment_Display u_7_segment_display_3 (
    .g(maininternal_1_out_seg3_g), .f(maininternal_1_out_seg3_f), .a(maininternal_1_out_seg3_a),
    .b(maininternal_1_out_seg3_b), .e(maininternal_1_out_seg3_e), .d(maininternal_1_out_seg3_d),
    .c(maininternal_1_out_seg3_c));  // open: dp
  _7_Segment_Display Result (
    .g(maininternal_1_out_seg2_g), .f(maininternal_1_out_seg2_f), .a(maininternal_1_out_seg2_a),
    .b(maininternal_1_out_seg2_b), .e(maininternal_1_out_seg2_e), .d(maininternal_1_out_seg2_d),
    .c(maininternal_1_out_seg2_c));  // open: dp
  LED led_121 (.in(maininternal_1_mar_led5));
  LED led_122 (.in(maininternal_1_mar_led3));
  LED led_123 (.in(maininternal_1_mar_led4));
  LED led_124 (.in(maininternal_1_mar_led6));
  LED led_125 (.in(maininternal_1_ram_led6));
  LED led_126 (.in(maininternal_1_ram_led5));
  LED led_127 (.in(maininternal_1_ram_led3));
  LED led_128 (.in(maininternal_1_ram_led4));
  _7_Segment_Display u_7_segment_display_4 (
    .g(maininternal_1_out_seg1_g), .f(maininternal_1_out_seg1_f), .a(maininternal_1_out_seg1_a),
    .b(maininternal_1_out_seg1_b), .e(maininternal_1_out_seg1_e), .d(maininternal_1_out_seg1_d),
    .c(maininternal_1_out_seg1_c));  // open: dp
  _7_Segment_Display u_7_segment_display_5 (
    .g(maininternal_1_out_seg0_g), .f(maininternal_1_out_seg0_f), .a(maininternal_1_out_seg0_a),
    .b(maininternal_1_out_seg0_b), .e(maininternal_1_out_seg0_e), .d(maininternal_1_out_seg0_d),
    .c(maininternal_1_out_seg0_c));  // open: dp
  LED led_129 (.in(maininternal_1_mar_led0));
  LED led_130 (.in(maininternal_1_mar_led2));
  LED led_131 (.in(maininternal_1_mar_led1));
  LED led_132 (.in(maininternal_1_ram_led0));
  LED led_133 (.in(maininternal_1_ram_led2));
  LED led_134 (.in(maininternal_1_ram_led1));
endmodule

module partCLK (
  input  Pulse,
  input  Mode,
  input  HLT,
  output LED,
  output CLK,
  output CLK_7d3332a1
);

  wire and_1_out, and_2_out, Auto_out, not_1_out, not_2_out, or_1_out;

  Clock Auto (.out(Auto_out));
  not not_1 (not_1_out, Mode);
  not not_2 (not_2_out, HLT);
  and and_1 (and_1_out, Auto_out, Mode);
  or or_1 (or_1_out, and_1_out, and_2_out);
  and and_2 (and_2_out, not_1_out, Pulse);
  and and_3 (CLK, or_1_out, not_2_out);
  not not_3 (CLK_7d3332a1, CLK);

  assign LED = CLK;
endmodule

module partPC (
  input  CO_d457f91e,
  input  CLR_b6b4cc54,
  input  CLK,
  input  [11:0] BusI,
  input  J_ab0d5ac6,
  input  CE,
  output [11:0] BusO,
  output TerminalCount,
  output [11:0] LEDs
);

  wire ic74xx161_2_tc, ic74xx161_3_tc;
  wire [7:4] ic74xx245_2_bo, undriven;

  ic74xx245 ic74xx245_1 (.EO_9639ac40(CO_d457f91e), .BI(LEDs[7:0]), .DIR(1'b0), .BO(BusO[7:0]));  // open: AO, AI
  ic74xx245 ic74xx245_2 (
    .EO_9639ac40(CO_d457f91e), .BI({undriven, LEDs[11:8]}), .DIR(1'b0), .BO({ic74xx245_2_bo, BusO[11:8]}));  // open: AO, AI
  ic74xx161 ic74xx161_1 (
    .Q0(LEDs[8]), .D3(BusI[11]), .MR_41874348(CLR_b6b4cc54), .D2(BusI[10]), .TC(TerminalCount), .CEP(CE),
    .CP(CLK), .D1(BusI[9]), .PE_5306d61a(J_ab0d5ac6), .CET(ic74xx161_2_tc), .D0(BusI[8]), .Q1(LEDs[9]),
    .Q2(LEDs[10]), .Q3(LEDs[11]));
  ic74xx161 ic74xx161_2 (
    .Q0(LEDs[4]), .D3(BusI[7]), .MR_41874348(CLR_b6b4cc54), .D2(BusI[6]), .TC(ic74xx161_2_tc), .CEP(CE),
    .CP(CLK), .D1(BusI[5]), .PE_5306d61a(J_ab0d5ac6), .CET(ic74xx161_3_tc), .D0(BusI[4]), .Q1(LEDs[5]),
    .Q2(LEDs[6]), .Q3(LEDs[7]));
  ic74xx161 ic74xx161_3 (
    .Q0(LEDs[0]), .D3(BusI[3]), .MR_41874348(CLR_b6b4cc54), .D2(BusI[2]), .TC(ic74xx161_3_tc), .CEP(CE),
    .CP(CLK), .D1(BusI[1]), .PE_5306d61a(J_ab0d5ac6), .CET(CE), .D0(BusI[0]), .Q1(LEDs[1]), .Q2(LEDs[2]),
    .Q3(LEDs[3]));
endmodule

module partREG (
  input  xO_05de6390,
  input  CLR,
  input  CLK,
  input  xI_9c528b91,
  input  [15:0] BusI,
  output [15:0] BusO,
  output [15:0] RegO,
  output [15:0] LEDs
);

  ic74xx245 ic74xx245_1 (.EO_9639ac40(xO_05de6390), .BI(LEDs[7:0]), .DIR(1'b0), .BO(BusO[7:0]));  // open: AO, AI
  ic74xx245 ic74xx245_2 (.EO_9639ac40(xO_05de6390), .BI(LEDs[15:8]), .DIR(1'b0), .BO(BusO[15:8]));  // open: AO, AI
  ic74xx173 ic74xx173_1 (
    .CLR(CLR), .N_edc11205(1'b0), .G2_ba7b7058(xI_9c528b91), .D(BusI[3:0]), .M_5f199db6(1'b0), .CLK(CLK),
    .G1_eeaaf593(xI_9c528b91), .Q(LEDs[3:0]));
  ic74xx173 ic74xx173_2 (
    .CLR(CLR), .N_edc11205(1'b0), .G2_ba7b7058(xI_9c528b91), .D(BusI[7:4]), .M_5f199db6(1'b0), .CLK(CLK),
    .G1_eeaaf593(xI_9c528b91), .Q(LEDs[7:4]));
  ic74xx173 ic74xx173_3 (
    .CLR(CLR), .N_edc11205(1'b0), .G2_ba7b7058(xI_9c528b91), .D(BusI[11:8]), .M_5f199db6(1'b0), .CLK(CLK),
    .G1_eeaaf593(xI_9c528b91), .Q(LEDs[11:8]));
  ic74xx173 ic74xx173_4 (
    .CLR(CLR), .N_edc11205(1'b0), .G2_ba7b7058(xI_9c528b91), .D(BusI[15:12]), .M_5f199db6(1'b0), .CLK(CLK),
    .G1_eeaaf593(xI_9c528b91), .Q(LEDs[15:12]));

  assign RegO = LEDs;
endmodule

module partALU (
  input  EO_a0c37f53,
  input  SU,
  input  XR,
  input  R,
  input  AN,
  input  NT,
  input  [15:0] A,
  input  [15:0] B,
  input  CLR,
  input  FI_261165dc,
  input  CLK,
  output [15:0] RES_LEDs,
  output [15:0] BusO,
  output Overflow,
  output CF_LED,
  output ZF_LED,
  output CF,
  output ZF
);

  wire AD_out, nand_1_out, not_1_out, not_2_out, or_2_out;
  wire [2:0] or_1_out;
  wire [3:0] sub16bitalu_1_p6;
  wire [3:2] ic74xx173_1_q;
  wire [7:0] pull_resistor_1_node, pull_resistor_1_node_2;
  wire [15:0] not_3_out, sub16bitalu_1_p7;

  nor AD (AD_out, AN, R, XR, SU, NT);
  or or_1 (or_1_out[0], AD_out, R);
  not not_1 (not_1_out, AN);
  nand nand_1 (nand_1_out, not_1_out, or_2_out);
  or or_2 (or_2_out, XR, R);
  or or_3 (or_1_out[2], XR, AN, R);
  xor xor_1 (or_1_out[1], NT, nand_1_out);
  not not_2 (not_2_out, NT);
  ic74xx245 ic74xx245_1 (.EO_9639ac40(EO_a0c37f53), .BI(RES_LEDs[7:0]), .DIR(1'b0), .BO(BusO[7:0]));  // open: AO, AI
  ic74xx245 ic74xx245_2 (.EO_9639ac40(EO_a0c37f53), .BI(RES_LEDs[15:8]), .DIR(1'b0), .BO(BusO[15:8]));  // open: AO, AI
  assign not_3_out = ~A;  // NOT_Gate not_3, 16 bits wide
  // sub16bitALU sub16bitalu_1: pin names not known; wires that end beside it: A, B, SU, or_1_out, Overflow, sub16bitalu_1_p6[0], sub16bitalu_1_p7
  assign RES_LEDs = sub16bitalu_1_p7 | {pull_resistor_1_node_2, pull_resistor_1_node};  // OR_Gate or_4, 16 bits wide
  Pull_Resistor pull_resistor_1 (.node({pull_resistor_1_node_2, pull_resistor_1_node}));
  ic74xx245 ic74xx245_3 (
    .EO_9639ac40(not_2_out), .AO(pull_resistor_1_node), .DIR(1'b1), .AI(not_3_out[7:0]));  // open: BI, BO
  ic74xx245 ic74xx245_4 (
    .EO_9639ac40(not_2_out), .AO(pull_resistor_1_node_2), .DIR(1'b1), .AI(not_3_out[15:8]));  // open: BI, BO
  ic74xx173 ic74xx173_1 (
    .CLR(CLR), .N_edc11205(1'b0), .G2_ba7b7058(FI_261165dc), .D(sub16bitalu_1_p6), .M_5f199db6(1'b0),
    .CLK(CLK), .G1_eeaaf593(FI_261165dc), .Q({ic74xx173_1_q, ZF, CF}));
  nor nor_1 (sub16bitalu_1_p6[1], RES_LEDs[0], RES_LEDs[1], RES_LEDs[2], RES_LEDs[3], RES_LEDs[4], RES_LEDs[5], RES_LEDs[6], RES_LEDs[7], RES_LEDs[9], RES_LEDs[10], RES_LEDs[11], RES_LEDs[12], RES_LEDs[13], RES_LEDs[14], RES_LEDs[15], RES_LEDs[8]);

  assign CF_LED = CF;
  assign ZF_LED = ZF;

  // Notes on the sheet:
  //   ZERO Flag
endmodule

module partMAR (
  input  [11:0] BusI,
  input  CLR,
  input  MI_85f63c41,
  input  CLK,
  input  [11:0] AddrSWs_d391c16e,
  input  Mode,
  output [11:0] A,
  output [11:0] A_LEDs,
  output RunLED,
  output ProgLED,
  output PROG
);

  wire [3:0] ic74xx173_1_q, ic74xx173_2_q, ic74xx173_3_q;

  ic74xx157 ic74xx157_1 (.Zx(A[3:0]), .I1x(ic74xx173_1_q), .I0x(AddrSWs_d391c16e[3:0]), .S(RunLED), .E_cd580d55(1'b0));
  ic74xx157 ic74xx157_2 (.Zx(A[7:4]), .I1x(ic74xx173_2_q), .I0x(AddrSWs_d391c16e[7:4]), .S(RunLED), .E_cd580d55(1'b0));
  ic74xx157 ic74xx157_3 (
    .Zx(A[11:8]), .I1x(ic74xx173_3_q), .I0x(AddrSWs_d391c16e[11:8]), .S(RunLED), .E_cd580d55(1'b0));
  not not_1 (RunLED, Mode);
  ic74xx173 ic74xx173_1 (
    .CLR(CLR), .N_edc11205(1'b0), .G2_ba7b7058(MI_85f63c41), .D(BusI[3:0]), .M_5f199db6(1'b0), .CLK(CLK),
    .G1_eeaaf593(MI_85f63c41), .Q(ic74xx173_1_q));
  ic74xx173 ic74xx173_2 (
    .CLR(CLR), .N_edc11205(1'b0), .G2_ba7b7058(MI_85f63c41), .D(BusI[7:4]), .M_5f199db6(1'b0), .CLK(CLK),
    .G1_eeaaf593(MI_85f63c41), .Q(ic74xx173_2_q));
  ic74xx173 ic74xx173_3 (
    .CLR(CLR), .N_edc11205(1'b0), .G2_ba7b7058(MI_85f63c41), .D(BusI[11:8]), .M_5f199db6(1'b0), .CLK(CLK),
    .G1_eeaaf593(MI_85f63c41), .Q(ic74xx173_3_q));

  assign A_LEDs = A;
  assign PROG = Mode;
  assign ProgLED = Mode;
endmodule

module partRAM (
  input  [11:0] A,
  input  CLR,
  input  RO_b3172779,
  input  [15:0] BusI,
  input  PROG,
  input  [15:0] ProgSW,
  input  ProgOK,
  input  RI,
  input  CLK,
  output [15:0] LEDs,
  output [15:0] BusO
);

  wire CLK_d3cc9788_out, not_1_out, not_2_out, not_3_out, not_5_out;
  wire [3:0] ic74xx157_1_zx, undriven, undriven_2;
  wire [15:0] LSB_zx;

  RAM #(.addrWidth(12), .dataWidth(16), .databus("bibus")) ram_1 (
    .addr(A), .we(not_1_out), .oe(not_2_out), .clk(not_3_out), .din(LSB_zx), .dout(LEDs));
  not not_1 (not_1_out, ic74xx157_1_zx[2]);
  not not_2 (not_2_out, 1'b0);
  not not_3 (not_3_out, CLK_d3cc9788_out);
  Clock CLK_d3cc9788 (.out(CLK_d3cc9788_out));
  not not_4 (undriven[2], ProgOK);
  ic74xx157 ic74xx157_1 (.Zx(ic74xx157_1_zx), .I1x(undriven_2), .I0x(undriven), .S(not_5_out), .E_cd580d55(1'b0));
  ic74xx245 ic74xx245_1 (.EO_9639ac40(RO_b3172779), .AO(BusO[7:0]), .DIR(1'b1), .AI(LEDs[7:0]));  // open: BI, BO
  ic74xx245 ic74xx245_2 (.EO_9639ac40(RO_b3172779), .AO(BusO[15:8]), .DIR(1'b1), .AI(LEDs[15:8]));  // open: BI, BO
  nand nand_1 (undriven_2[2], RI, CLK);
  not not_5 (not_5_out, PROG);
  ic74xx157 MSB (.Zx(LSB_zx[15:12]), .I1x(BusI[15:12]), .I0x(ProgSW[15:12]), .S(not_5_out), .E_cd580d55(1'b0));
  ic74xx157 ic74xx157_2 (.Zx(LSB_zx[11:8]), .I1x(BusI[11:8]), .I0x(ProgSW[11:8]), .S(not_5_out), .E_cd580d55(1'b0));
  ic74xx157 ic74xx157_3 (.Zx(LSB_zx[7:4]), .I1x(BusI[7:4]), .I0x(ProgSW[7:4]), .S(not_5_out), .E_cd580d55(1'b0));
  ic74xx157 LSB (.Zx(LSB_zx[3:0]), .I1x(BusI[3:0]), .I0x(ProgSW[3:0]), .S(not_5_out), .E_cd580d55(1'b0));
endmodule

module partIR (
  input  IO_a1d15099,
  input  CLR,
  input  CLK,
  input  II_193c5152,
  input  [15:0] BusI,
  output [15:0] BusO,
  output [15:0] LEDs,
  output [3:0] RegO
);

  ic74xx245 ic74xx245_1 (.EO_9639ac40(IO_a1d15099), .BI(LEDs[7:0]), .DIR(1'b0), .BO(BusO[7:0]));  // open: AO, AI
  ic74xx245 ic74xx245_2 (
    .EO_9639ac40(IO_a1d15099), .BI({4'b0000, LEDs[11:8]}), .DIR(1'b0), .BO(BusO[15:8]));  // open: AO, AI
  ic74xx173 ic74xx173_1 (
    .CLR(CLR), .N_edc11205(1'b0), .G2_ba7b7058(II_193c5152), .D(BusI[3:0]), .M_5f199db6(1'b0), .CLK(CLK),
    .G1_eeaaf593(II_193c5152), .Q(LEDs[3:0]));
  ic74xx173 ic74xx173_2 (
    .CLR(CLR), .N_edc11205(1'b0), .G2_ba7b7058(II_193c5152), .D(BusI[7:4]), .M_5f199db6(1'b0), .CLK(CLK),
    .G1_eeaaf593(II_193c5152), .Q(LEDs[7:4]));
  ic74xx173 ic74xx173_3 (
    .CLR(CLR), .N_edc11205(1'b0), .G2_ba7b7058(II_193c5152), .D(BusI[11:8]), .M_5f199db6(1'b0), .CLK(CLK),
    .G1_eeaaf593(II_193c5152), .Q(LEDs[11:8]));
  ic74xx173 ic74xx173_4 (
    .CLR(CLR), .N_edc11205(1'b0), .G2_ba7b7058(II_193c5152), .D(BusI[15:12]), .M_5f199db6(1'b0), .CLK(CLK),
    .G1_eeaaf593(II_193c5152), .Q(LEDs[15:12]));

  assign RegO = LEDs[15:12];
endmodule

module partCTRL (
  input  CLK_0416f44f,
  input  [3:0] RegI,
  input  CFI,
  input  ZFI,
  input  Reset,
  output AO_fda11864,
  output AI_f325b2de,
  output II_51e65cc3,
  output IO_06df68e4,
  output RO_f7a11c4b,
  output RI,
  output MI_1a8064a7,
  output HLT,
  output [2:0] Count_LEDs,
  output FI_fa84cb50,
  output J_e6dac3f4,
  output CLR_87b95d37,
  output [4:0] Time_LEDs_backwards,
  output CO_e8fa446c,
  output CE,
  output CLR,
  output OI,
  output BI_dc5a9e0c,
  output SU,
  output EO_bf3b4110,
  output [19:0] CTRL_LEDs,
  output NT,
  output AN,
  output R,
  output XR
);

  wire ic74xx138_1_q5, nand_1_out, nand_2_out;
  wire [4:0] ic74xx138_1_q0;
  wire [7:4] Controls2_data;

  nand nand_1 (nand_1_out, nand_2_out, nand_2_out);
  nand nand_2 (nand_2_out, ic74xx138_1_q5, CLR_87b95d37);
  nand nand_3 (CLR_87b95d37, Reset, Reset);
  ic74xx138 ic74xx138_1 (
    .Q3(ic74xx138_1_q0[3]), .Q4(ic74xx138_1_q0[4]), .Q5(ic74xx138_1_q5), .A0(Count_LEDs[0]),
    .A1(Count_LEDs[1]), .A2(Count_LEDs[2]), .E3(1'b1), .E2_81dff10d(1'b0), .E1_52d9cec0(1'b0),
    .Q2(ic74xx138_1_q0[2]), .Q1(ic74xx138_1_q0[1]), .Q0(ic74xx138_1_q0[0]));  // open: Q6, Q7
  nand nand_4 (CLR, CLR_87b95d37, CLR_87b95d37);
  ic74xx161 ic74xx161_1 (
    .Q0(Count_LEDs[0]), .MR_41874348(nand_1_out), .CEP(1'b1), .CP(CLK_0416f44f), .PE_5306d61a(1'b1),
    .CET(1'b1), .Q1(Count_LEDs[1]), .Q2(Count_LEDs[2]));  // open: D3, D2, TC, D1, D0, Q3
  assign Time_LEDs_backwards = ~ic74xx138_1_q0;  // NOT_Gate not_1, 5 bits wide
  ROM #(.addrWidth(9)) Controls0 (
    .addr({ZFI, CFI, RegI, Count_LEDs}),
    .data({AO_fda11864, AI_f325b2de, II_51e65cc3, IO_06df68e4, RO_f7a11c4b, CTRL_LEDs[2], MI_1a8064a7, CTRL_LEDs[0]}));
  ROM #(.addrWidth(9)) Controls1 (
    .addr({ZFI, CFI, RegI, Count_LEDs}),
    .data({FI_fa84cb50, J_e6dac3f4, CO_e8fa446c, CE, CTRL_LEDs[11], BI_dc5a9e0c, CTRL_LEDs[9], EO_bf3b4110}));
  ROM #(.addrWidth(9)) Controls2 (
    .addr({ZFI, CFI, RegI, Count_LEDs}), .data({Controls2_data, CTRL_LEDs[19], AN, CTRL_LEDs[17:16]}));
  not not_2 (CTRL_LEDs[1], MI_1a8064a7);
  not not_3 (CTRL_LEDs[4], IO_06df68e4);
  not not_4 (CTRL_LEDs[3], RO_f7a11c4b);
  not not_5 (CTRL_LEDs[8], EO_bf3b4110);
  not not_6 (CTRL_LEDs[10], BI_dc5a9e0c);
  not not_7 (CTRL_LEDs[5], II_51e65cc3);
  not not_8 (CTRL_LEDs[6], AI_f325b2de);
  not not_9 (CTRL_LEDs[7], AO_fda11864);
  not not_10 (CTRL_LEDs[13], CO_e8fa446c);
  not not_11 (CTRL_LEDs[14], J_e6dac3f4);
  not not_12 (CTRL_LEDs[15], FI_fa84cb50);

  assign {CTRL_LEDs[18], CTRL_LEDs[12]} = {AN, CE};
  assign HLT = CTRL_LEDs[0];
  assign NT = CTRL_LEDs[19];
  assign OI = CTRL_LEDs[11];
  assign R = CTRL_LEDs[17];
  assign RI = CTRL_LEDs[2];
  assign SU = CTRL_LEDs[9];
  assign XR = CTRL_LEDs[16];

  // Notes on the sheet:
  //   contents of Controls0 (hex, n*v repeats v):
  //   f8 d2 fa fa fa 0 0 0 f8 d2 e8 b2 fa 0 0 0 f8 d2 e8 f2 ba 0 0 0 f8 d2 e8 f2 ba 0 0 0 f8 d2 e8 7e fa 0
  //   0 0 f8 d2 aa fa fa 0 0 0 f8 d2 ea fa fa 0 0 0 f8 d2 fa fa fa 0 0 0 f8 d2 fa fa fa 0 0 0 f8 d2 e8 f2
  //   ba 0 0 0 f8 d2 e8 f2 ba 0 0 0 f8 d2 e8 f2 ba 0 0 0 f8 d2 ba fa fa 0 0 0 f8 d2 fa fa fa 0 0 0 f8 d2
  //   7a fa fa 0 0 0 f8 d2 fb fa fa 0 0 0 f8 d2 fa fa fa 0 0 0 f8 d2 e8 b2 fa 0 0 0 f8 d2 e8 f2 ba 0 0 0
  //   f8 d2 e8 f2 ba 0 0 0 f8 d2 e8 7e fa 0 0 0 f8 d2 aa fa fa 0 0 0 f8 d2 ea fa fa 0 0 0 f8 d2 ea fa fa 0
  //   0 0 f8 d2 fa fa fa 0 0 0 f8 d2 e8 f2 ba 0 0 0 f8 d2 e8 f2 ba 0 0 0 f8 d2 e8 f2 ba 0 0 0 f8 d2 ba fa
  //   fa 0 0 0 f8 d2 fa fa fa 0 0 0 f8 d2 7a fa fa 0 0 0 f8 d2 fb fa fa 0 0 0 f8 d2 fa fa fa 0 0 0 f8 d2
  //   e8 b2 fa 0 0 0 f8 d2 e8 f2 ba 0 0 0 f8 d2 e8 f2 ba 0 0 0 f8 d2 e8 7e fa 0 0 0 f8 d2 aa fa fa 0 0 0
  //   f8 d2 ea fa fa 0 0 0 f8 d2 fa fa fa 0 0 0 f8 d2 ea fa fa 0 0 0 f8 d2 e8 f2 ba 0 0 0 f8 d2 e8 f2 ba 0
  //   0 0 f8 d2 e8 f2 ba 0 0 0 f8 d2 ba fa fa 0 0 0 f8 d2 fa fa fa 0 0 0 f8 d2 7a fa fa 0 0 0 f8 d2 fb fa
  //   fa 0 0 0 f8 d2 fa fa fa 0 0 0 f8 d2 e8 b2 fa 0 0 0 f8 d2 e8 f2 ba 0 0 0 f8 d2 e8 f2 ba 0 0 0 f8 d2
  //   e8 7e fa 0 0 0 f8 d2 aa fa fa 0 0 0 f8 d2 ea fa fa 0 0 0 f8 d2 ea fa fa 0 0 0 f8 d2 ea fa fa 0 0 0
  //   f8 d2 e8 f2 ba 0 0 0 f8 d2 e8 f2 ba 0 0 0 f8 d2 e8 f2 ba 0 0 0 f8 d2 ba fa fa 0 0 0 f8 d2 fa fa fa 0
  //   0 0 f8 d2 7a fa fa 0 0 0 f8 d2 fb fa fa
  //   contents of Controls1 (hex, n*v repeats v):
  //   c5 f5 e5 e5 e5 0 0 0 c5 f5 e5 e5 e5 0 0 0 c5 f5 e5 e1 64 0 0 0 c5 f5 e5 e1 66 0 0 0 c5 f5 e5 e5 e5 0
  //   0 0 c5 f5 e5 e5 e5 0 0 0 c5 f5 a5 e5 e5 0 0 0 c5 f5 e5 e5 e5 0 0 0 c5 f5 e5 e5 e5 0 0 0 c5 f5 e5 e1
  //   64 0 0 0 c5 f5 e5 e1 64 0 0 0 c5 f5 e5 e1 64 0 0 0 c5 f5 64 e5 e5 0 0 0 c5 f5 e5 e5 e5 0 0 0 c5 f5
  //   ed e5 e5 0 0 0 c5 f5 e5 e5 e5 0 0 0 c5 f5 e5 e5 e5 0 0 0 c5 f5 e5 e5 e5 0 0 0 c5 f5 e5 e1 64 0 0 0
  //   c5 f5 e5 e1 66 0 0 0 c5 f5 e5 e5 e5 0 0 0 c5 f5 e5 e5 e5 0 0 0 c5 f5 a5 e5 e5 0 0 0 c5 f5 a5 e5 e5 0
  //   0 0 c5 f5 e5 e5 e5 0 0 0 c5 f5 e5 e1 64 0 0 0 c5 f5 e5 e1 64 0 0 0 c5 f5 e5 e1 64 0 0 0 c5 f5 64 e5
  //   e5 0 0 0 c5 f5 e5 e5 e5 0 0 0 c5 f5 ed e5 e5 0 0 0 c5 f5 e5 e5 e5 0 0 0 c5 f5 e5 e5 e5 0 0 0 c5 f5
  //   e5 e5 e5 0 0 0 c5 f5 e5 e1 64 0 0 0 c5 f5 e5 e1 66 0 0 0 c5 f5 e5 e5 e5 0 0 0 c5 f5 e5 e5 e5 0 0 0
  //   c5 f5 a5 e5 e5 0 0 0 c5 f5 e5 e5 e5 0 0 0 c5 f5 a5 e5 e5 0 0 0 c5 f5 e5 e1 64 0 0 0 c5 f5 e5 e1 64 0
  //   0 0 c5 f5 e5 e1 64 0 0 0 c5 f5 64 e5 e5 0 0 0 c5 f5 e5 e5 e5 0 0 0 c5 f5 ed e5 e5 0 0 0 c5 f5 e5 e5
  //   e5 0 0 0 c5 f5 e5 e5 e5 0 0 0 c5 f5 e5 e5 e5 0 0 0 c5 f5 e5 e1 64 0 0 0 c5 f5 e5 e1 66 0 0 0 c5 f5
  //   e5 e5 e5 0 0 0 c5 f5 e5 e5 e5 0 0 0 c5 f5 a5 e5 e5 0 0 0 c5 f5 a5 e5 e5 0 0 0 c5 f5 a5 e5 e5 0 0 0
  //   c5 f5 e5 e1 64 0 0 0 c5 f5 e5 e1 64 0 0 0 c5 f5 e5 e1 64 0 0 0 c5 f5 64 e5 e5 0 0 0 c5 f5 e5 e5 e5 0
  //   0 0 c5 f5 ed e5 e5 0 0 0 c5 f5 e5 e5 e5
  //   contents of Controls2 (hex, n*v repeats v):
  //   76*0 1 7*0 2 7*0 4 5*0 8 105*0 1 7*0 2 7*0 4 5*0 8 105*0 1 7*0 2 7*0 4 5*0 8 105*0 1 7*0 2 7*0 4 5*0
  //   8
endmodule

module partOUT (
  input  OI,
  input  CLR_898658ba,
  input  CLK,
  input  Twos,
  input  Hex,
  input  [15:0] BusI,
  output [6:0] SSeg3,
  output [6:0] SSeg2,
  output [6:0] SSeg1,
  output [6:0] SSeg0
);

  wire and_1_out, subatmegahex_1_mplex0, subatmegahex_1_mplex1, subatmegahex_1_mplex2, subatmegahex_1_mplex3,
       subatmegahex_1_neg, subatmegahex_1_showzero;
  wire [6:0] subatmegahex_1_hex0, subatmegahex_1_hex1, subatmegahex_1_hex2, subatmegahex_1_hex3;
  wire [7:0] ic74xx273_1_q0, ic74xx273_2_q0;

  and and_1 (and_1_out, CLK, OI);
  ic74xx273 ic74xx273_1 (
    .Q2(ic74xx273_1_q0[2]), .D1(BusI[1]), .MR_b7c3316e(CLR_898658ba), .D4(BusI[4]), .D6(BusI[6]),
    .D7(BusI[7]), .D3(BusI[3]), .Q0(ic74xx273_1_q0[0]), .D0(BusI[0]), .Q1(ic74xx273_1_q0[1]), .D2(BusI[2]),
    .CP(and_1_out), .D5(BusI[5]), .Q3(ic74xx273_1_q0[3]), .Q4(ic74xx273_1_q0[4]), .Q5(ic74xx273_1_q0[5]),
    .Q6(ic74xx273_1_q0[6]), .Q7(ic74xx273_1_q0[7]));
  ic74xx273 ic74xx273_2 (
    .Q2(ic74xx273_2_q0[2]), .D1(BusI[9]), .MR_b7c3316e(CLR_898658ba), .D4(BusI[12]), .D6(BusI[14]),
    .D7(BusI[15]), .D3(BusI[11]), .Q0(ic74xx273_2_q0[0]), .D0(BusI[8]), .Q1(ic74xx273_2_q0[1]),
    .D2(BusI[10]), .CP(and_1_out), .D5(BusI[13]), .Q3(ic74xx273_2_q0[3]), .Q4(ic74xx273_2_q0[4]),
    .Q5(ic74xx273_2_q0[5]), .Q6(ic74xx273_2_q0[6]), .Q7(ic74xx273_2_q0[7]));
  assign SSeg3 = 1'b1 ? subatmegahex_1_hex3 : 7'bz;  // Controlled_Buffer controlled_buffer_1
  assign SSeg2 = 1'b1 ? subatmegahex_1_hex2 : 7'bz;  // Controlled_Buffer controlled_buffer_2
  subATmegaHex subatmegahex_1 (
    .Neg(subatmegahex_1_neg), .BUSIN({ic74xx273_2_q0, ic74xx273_1_q0}), .ShowZero(subatmegahex_1_showzero),
    .Hex(Hex), .CLK(CLK), .EN(1'b1), .MPlex0(subatmegahex_1_mplex0), .Twos(Twos),
    .RST_2e3f89a5(CLR_898658ba), .MPlex1(subatmegahex_1_mplex1), .MPlex2(subatmegahex_1_mplex2),
    .MPlex3(subatmegahex_1_mplex3), .Hex0(subatmegahex_1_hex0), .Hex1(subatmegahex_1_hex1),
    .Hex2(subatmegahex_1_hex2), .Hex3(subatmegahex_1_hex3));
  assign SSeg1 = 1'b1 ? subatmegahex_1_hex1 : 7'bz;  // Controlled_Buffer controlled_buffer_3
  LED Neg (.in(subatmegahex_1_neg));
  LED ShowZ (.in(subatmegahex_1_showzero));
  assign SSeg0 = 1'b1 ? subatmegahex_1_hex0 : 7'bz;  // Controlled_Buffer controlled_buffer_4
endmodule

module sub16bitALU (
  input  [15:0] A,
  input  [15:0] B,
  input  Mode,
  input  CIN,
  input  [3:0] SEL,
  output A_B,
  output COUT,
  output [15:0] SUM
);

  wire ic74xx181_3_cn4, ic74xx181_5_cn4, ic74xx181_7_p13, ic74xx181_7_p21;

  ic74xx181 ic74xx181_1 ();  // open: Cn4, G_, Cn, M, A0_, B0_, A1_, B1_, A2_, B2_, A3_, B3_, S0, S1, S2, S3, P_, F3_, F2_, A_B, F1_, F0_
  ic74xx181 ic74xx181_2 (
    .Cn4(COUT), .Cn(ic74xx181_3_cn4), .M(Mode), .A0_(A[0]), .B0_(B[0]), .A1_(A[1]), .B1_(B[1]), .A2_(A[2]),
    .B2_(B[2]), .A3_(A[3]), .B3_(B[3]), .S0(SEL[0]), .S1(SEL[1]), .S2(SEL[2]), .S3(SEL[3]), .F3_(SUM[3]),
    .F2_(SUM[2]), .F1_(SUM[1]), .F0_(SUM[0]));  // open: G_, P_, A_B
  // Probe on A
  // Probe on A
  ic74xx181 ic74xx181_3 (
    .Cn4(ic74xx181_3_cn4), .Cn(ic74xx181_5_cn4), .M(Mode), .A0_(A[4]), .B0_(B[4]), .A1_(A[5]), .B1_(B[5]),
    .A2_(A[6]), .B2_(B[6]), .A3_(A[7]), .B3_(B[7]), .S0(SEL[0]), .S1(SEL[1]), .S2(SEL[2]), .S3(SEL[3]),
    .F3_(SUM[7]), .F2_(SUM[6]), .F1_(SUM[5]), .F0_(SUM[4]));  // open: G_, P_, A_B
  ic74xx181 ic74xx181_4 ();  // open: Cn4, G_, Cn, M, A0_, B0_, A1_, B1_, A2_, B2_, A3_, B3_, S0, S1, S2, S3, P_, F3_, F2_, A_B, F1_, F0_
  // Probe on SUM
  ic74xx182 ic74xx182_1 ();  // open: CnY_, CnX_, P3, G3, P2, G2, P1, G1, Cn, P0, G0, CnZ_, G, P
  // Probe on B
  ic74xx181 ic74xx181_5 (
    .Cn4(ic74xx181_5_cn4), .Cn(ic74xx181_7_p21), .M(Mode), .A0_(A[8]), .B0_(B[8]), .A1_(A[9]), .B1_(B[9]),
    .A2_(A[10]), .B2_(B[10]), .A3_(A[11]), .B3_(B[11]), .S0(SEL[0]), .S1(SEL[1]), .S2(SEL[2]), .S3(SEL[3]),
    .F3_(SUM[11]), .F2_(SUM[10]), .F1_(SUM[9]), .F0_(SUM[8]));  // open: G_, P_, A_B
  // Probe on SUM
  ic74xx181 ic74xx181_6 ();  // open: Cn4, G_, Cn, M, A0_, B0_, A1_, B1_, A2_, B2_, A3_, B3_, S0, S1, S2, S3, P_, F3_, F2_, A_B, F1_, F0_
  // Probe on B
  // ic74xx181 ic74xx181_7: pin names not known; wires that end beside it: A[12], A[13], A[14], A[15], B[12], B[13], B[14], B[15], SEL[0], SEL[1], SEL[2], SEL[3], ic74xx181_7_p13, ic74xx181_7_p13, Mode, CIN, SUM[12], SUM[13], SUM[14], SUM[15], ic74xx181_7_p21, A_B
  ic74xx181 ic74xx181_8 ();  // open: Cn4, G_, Cn, M, A0_, B0_, A1_, B1_, A2_, B2_, A3_, B3_, S0, S1, S2, S3, P_, F3_, F2_, A_B, F1_, F0_
endmodule

module subATmegaHex (
  input  Twos,
  input  Hex,
  input  [15:0] BUSIN,
  input  EN,
  input  RST_2e3f89a5,
  input  CLK,
  output Neg,
  output ShowZero,
  output MPlex0,
  output MPlex1,
  output MPlex2,
  output MPlex3,
  output [6:0] Hex0,
  output [6:0] Hex1,
  output [6:0] Hex2,
  output [6:0] Hex3
);

  wire and_1_out, ic74xx139_1_o0a, ic74xx139_1_o1a, ic74xx139_1_o2a, ic74xx139_1_o3a, ic74xx161_1_q0,
       ic74xx161_1_q1, MplexCLK_out, not_1_out, not_6_out, not_7_out;
  wire [3:0] controlled_buffer_1_out, controlled_buffer_2_out, controlled_buffer_3_out,
       controlled_buffer_4_out, ic74xx173_1_q, ic74xx173_2_q, ic74xx173_3_q, ic74xx173_4_q;
  wire [15:0] and_4_out;

  ROM #(.addrWidth(4), .dataWidth(7)) BinHex0 (.addr(controlled_buffer_1_out), .data(Hex0));
  ROM #(.addrWidth(4), .dataWidth(7)) BinHex1 (.addr(controlled_buffer_2_out), .data(Hex1));
  ROM #(.addrWidth(4), .dataWidth(7)) BinHex2 (.addr(controlled_buffer_3_out), .data(Hex2));
  ROM #(.addrWidth(4), .dataWidth(7)) BinHex3 (.addr(controlled_buffer_4_out), .data(Hex3));
  Clock MplexCLK (.out(MplexCLK_out));
  and and_1 (and_1_out, MplexCLK_out, EN);
  ic74xx161 ic74xx161_1 (
    .Q0(ic74xx161_1_q0), .MR_41874348(RST_2e3f89a5), .CEP(EN), .CP(and_1_out), .PE_5306d61a(EN), .CET(EN),
    .Q1(ic74xx161_1_q1));  // open: D3, D2, TC, D1, D0, Q2, Q3
  and and_2 (ShowZero, Hex, EN, RST_2e3f89a5);
  and and_3 (Neg, Twos, EN, RST_2e3f89a5);
  not not_1 (not_1_out, EN);
  assign and_4_out = BUSIN & {16{EN}} & {16{RST_2e3f89a5}};  // AND_Gate and_4, 16 bits wide
  ic74xx139 ic74xx139_1 (
    .O3a(ic74xx139_1_o3a), .O2a(ic74xx139_1_o2a), .O1a(ic74xx139_1_o1a), .O0a(ic74xx139_1_o0a),
    .A1a(ic74xx161_1_q1), .A0a(ic74xx161_1_q0), .Ea_27b583f7(not_1_out));  // open: O0b, A1b, A0b, Eb_4802ef8e, O1b, O2a_2, O3b
  not not_2 (MPlex0, ic74xx139_1_o0a);
  assign controlled_buffer_1_out = 1'b1 ? ic74xx173_1_q : 4'bz;  // Controlled_Buffer controlled_buffer_1
  not not_3 (MPlex1, ic74xx139_1_o1a);
  not not_4 (MPlex2, ic74xx139_1_o2a);
  not not_5 (MPlex3, ic74xx139_1_o3a);
  assign controlled_buffer_2_out = 1'b1 ? ic74xx173_2_q : 4'bz;  // Controlled_Buffer controlled_buffer_2
  assign controlled_buffer_3_out = 1'b1 ? ic74xx173_3_q : 4'bz;  // Controlled_Buffer controlled_buffer_3
  assign controlled_buffer_4_out = 1'b1 ? ic74xx173_4_q : 4'bz;  // Controlled_Buffer controlled_buffer_4
  not not_6 (not_6_out, RST_2e3f89a5);
  not not_7 (not_7_out, EN);
  ic74xx173 ic74xx173_1 (
    .CLR(not_6_out), .N_edc11205(1'b0), .G2_ba7b7058(not_7_out), .D(and_4_out[3:0]), .M_5f199db6(1'b0),
    .CLK(CLK), .G1_eeaaf593(not_7_out), .Q(ic74xx173_1_q));
  ic74xx173 ic74xx173_2 (
    .CLR(not_6_out), .N_edc11205(1'b0), .G2_ba7b7058(not_7_out), .D(and_4_out[7:4]), .M_5f199db6(1'b0),
    .CLK(CLK), .G1_eeaaf593(not_7_out), .Q(ic74xx173_2_q));
  ic74xx173 ic74xx173_3 (
    .CLR(not_6_out), .N_edc11205(1'b0), .G2_ba7b7058(not_7_out), .D(and_4_out[11:8]), .M_5f199db6(1'b0),
    .CLK(CLK), .G1_eeaaf593(not_7_out), .Q(ic74xx173_3_q));
  ic74xx173 ic74xx173_4 (
    .CLR(not_6_out), .N_edc11205(1'b0), .G2_ba7b7058(not_7_out), .D(and_4_out[15:12]), .M_5f199db6(1'b0),
    .CLK(CLK), .G1_eeaaf593(not_7_out), .Q(ic74xx173_4_q));

  // Notes on the sheet:
  //   contents of BinHex0 (hex, n*v repeats v):
  //   3f 6 5b 4f 66 6d 7d 7 7f 6f 77 7c 39 5e 79 71
  //   contents of BinHex1 (hex, n*v repeats v):
  //   3f 6 5b 4f 66 6d 7d 7 7f 6f 77 7c 39 5e 79 71
  //   contents of BinHex2 (hex, n*v repeats v):
  //   3f 6 5b 4f 66 6d 7d 7 7f 6f 77 7c 39 5e 79 71
  //   contents of BinHex3 (hex, n*v repeats v):
  //   3f 6 5b 4f 66 6d 7d 7 7f 6f 77 7c 39 5e 79 71
endmodule

module ic74xx138 (
  input  E1_52d9cec0,
  input  E2_81dff10d,
  input  E3,
  input  A2,
  input  A1,
  input  A0,
  output Q7,
  output Q6,
  output Q5,
  output Q4,
  output Q3,
  output Q2,
  output Q1,
  output Q0
);

  wire and_1_out, not_1_out, not_2_out, not_3_out, not_4_out, not_5_out, not_6_out, not_7_out, not_8_out;

  not not_1 (not_1_out, A2);
  not not_2 (not_2_out, not_1_out);
  nand nand_1 (Q7, not_2_out, not_6_out, not_5_out, and_1_out);
  not not_3 (not_3_out, A0);
  not not_4 (not_4_out, A1);
  not not_5 (not_5_out, not_4_out);
  not not_6 (not_6_out, not_3_out);
  nand nand_2 (Q6, and_1_out, not_5_out, not_2_out, not_3_out);
  nand nand_3 (Q5, and_1_out, not_6_out, not_2_out, not_4_out);
  nand nand_4 (Q4, and_1_out, not_2_out, not_4_out, not_3_out);
  not not_7 (not_7_out, E2_81dff10d);
  not not_8 (not_8_out, E1_52d9cec0);
  and and_1 (and_1_out, not_8_out, not_7_out, E3);
  nand nand_5 (Q3, and_1_out, not_1_out, not_5_out, not_6_out);
  nand nand_6 (Q1, and_1_out, not_1_out, not_4_out, not_6_out);
  nand nand_7 (Q2, and_1_out, not_1_out, not_5_out, not_3_out);
  nand nand_8 (Q0, and_1_out, not_1_out, not_4_out, not_3_out);
endmodule

module ic74xx139 (
  input  Ea_27b583f7,
  input  A0a,
  input  A1a,
  input  Eb_4802ef8e,
  input  A0b,
  input  A1b,
  output O0a,
  output O1a,
  output O2a,
  output O3a,
  output O0b,
  output O1b,
  output O2a_2,
  output O3b
);

  wire not_1_out, not_2_out, not_3_out, not_4_out, not_5_out, not_6_out, not_7_out, not_8_out, not_9_out;

  nand nand_1 (O0a, not_1_out, not_4_out, not_2_out);
  not not_1 (not_1_out, A0a);
  not not_2 (not_2_out, Ea_27b583f7);
  not not_3 (not_3_out, not_1_out);
  nand nand_2 (O2a, not_2_out, not_1_out, not_5_out);
  nand nand_3 (O1a, not_2_out, not_4_out, not_3_out);
  not not_4 (not_4_out, A1a);
  not not_5 (not_5_out, not_4_out);
  nand nand_4 (O0b, not_6_out, not_8_out, Eb_4802ef8e);
  nand nand_5 (O3a, not_2_out, not_5_out, not_3_out);
  not not_6 (not_6_out, A0b);
  not not_7 (not_7_out, not_6_out);
  nand nand_6 (O2a_2, Eb_4802ef8e, not_6_out, not_7_out);
  nand nand_7 (O1b, Eb_4802ef8e, not_8_out, not_7_out);
  not not_8 (not_8_out, A1b);
  not not_9 (not_9_out, not_8_out);
  nand nand_8 (O3b, Eb_4802ef8e, not_9_out, not_7_out);
endmodule

module ic74xx157 (
  input  E_cd580d55,
  input  S,
  input  [3:0] I0x,
  input  [3:0] I1x,
  output [3:0] Zx
);

  wire not_1_out, not_2_out;
  wire [3:0] and_1_out, and_2_out;
  wire [3:3] and_3_out, and_4_out;

  assign and_1_out = I0x & {4{and_3_out[3]}};  // AND_Gate and_1, 4 bits wide
  assign and_2_out = I1x & {4{and_4_out[3]}};  // AND_Gate and_2, 4 bits wide
  assign Zx = and_1_out | and_2_out;  // OR_Gate or_1, 4 bits wide
  not not_1 (not_1_out, E_cd580d55);
  not not_2 (not_2_out, S);
  and and_3 (and_3_out[3], not_1_out, not_2_out);
  and and_4 (and_4_out[3], not_1_out, S);
endmodule

module ic74xx161 (
  input  MR_41874348,
  input  CP,
  input  D0,
  input  D1,
  input  D2,
  input  D3,
  input  CEP,
  input  CET,
  input  PE_5306d61a,
  output TC,
  output Q0,
  output Q1,
  output Q2,
  output Q3
);

  wire and_1_out, counter_1_carry, not_1_out, not_2_out;

  not not_1 (not_1_out, MR_41874348);
  Counter #(.width(4), .max('hf)) counter_1 (
    .clr(not_1_out), .load(not_2_out), .up(and_1_out), .count(and_1_out), .clk(CP), .D({D3, D2, D1, D0}),
    .carry(counter_1_carry), .Q({Q3, Q2, Q1, Q0}));
  and and_1 (and_1_out, CEP, PE_5306d61a, CET);
  not not_2 (not_2_out, PE_5306d61a);
  and and_2 (TC, counter_1_carry, CET);

  // Notes on the sheet:
  //   74161: Synchronous 4-bit Binary Counter with Asynchronous Clear 
endmodule

module ic74xx173 (
  input  M_5f199db6,
  input  N_edc11205,
  input  G1_eeaaf593,
  input  G2_ba7b7058,
  input  [3:0] D,
  input  CLK,
  input  CLR,
  output [3:0] Q
);

  wire and_1_out, d_ff_1_qn, d_ff_2_qn, d_ff_3_qn, d_ff_4_qn, not_1_out, not_2_out, not_4_out;
  wire [3:0] and_3_out, and_4_out, d_ff_4_q, not_8_out, or_1_out;
  wire [3:3] and_2_out, not_3_out;

  and and_1 (and_1_out, M_5f199db6, N_edc11205);
  not not_1 (not_1_out, and_1_out);
  not not_2 (not_2_out, G1_eeaaf593);
  and and_2 (and_2_out[3], not_2_out, not_4_out);
  not not_3 (not_3_out[3], and_2_out[3]);
  not not_4 (not_4_out, G2_ba7b7058);
  assign and_3_out = {4{and_2_out[3]}} & D;  // AND_Gate and_3, 4 bits wide
  assign and_4_out = d_ff_4_q & {4{not_3_out[3]}};  // AND_Gate and_4, 4 bits wide
  assign or_1_out = and_4_out | and_3_out;  // OR_Gate or_1, 4 bits wide
  D_Flip_Flop d_ff_1 (.D(or_1_out[3]), .clk(CLK), .Q(d_ff_4_q[3]), .Qn(d_ff_1_qn), .reset(CLR));  // open: preset
  D_Flip_Flop d_ff_2 (.D(or_1_out[2]), .clk(CLK), .Q(d_ff_4_q[2]), .Qn(d_ff_2_qn), .reset(CLR));  // open: preset
  D_Flip_Flop d_ff_3 (.D(or_1_out[1]), .clk(CLK), .Q(d_ff_4_q[1]), .Qn(d_ff_3_qn), .reset(CLR));  // open: preset
  D_Flip_Flop d_ff_4 (.D(or_1_out[0]), .clk(CLK), .Q(d_ff_4_q[0]), .Qn(d_ff_4_qn), .reset(CLR));  // open: preset
  not not_5 (not_8_out[3], d_ff_1_qn);
  not not_6 (not_8_out[2], d_ff_2_qn);
  not not_7 (not_8_out[1], d_ff_3_qn);
  assign Q = not_1_out ? not_8_out : 4'bz;  // Controlled_Buffer controlled_buffer_1
  not not_8 (not_8_out[0], d_ff_4_qn);

  // Notes on the sheet:
  //   Output control
  //   Data enable
endmodule

module ic74xx181 (
  input  S3,
  input  S2,
  input  S1,
  input  S0,
  input  B3_,
  input  A3_,
  input  B2_,
  input  A2_,
  input  B1_,
  input  A1_,
  input  B0_,
  input  A0_,
  input  M,
  input  Cn,
  output G_,
  output Cn4,
  output P_,
  output F3_,
  output F2_,
  output A_B,
  output F1_,
  output F0_
);

  wire and_1_out, and_2_out, and_3_out, and_4_out, and_5_out, and_6_out, and_7_out, and_8_out, and_9_out,
       and_10_out, and_11_out, and_12_out, and_13_out, and_14_out, and_15_out, and_16_out, and_17_out,
       and_18_out, and_19_out, and_20_out, and_21_out, and_22_out, and_23_out, and_24_out, and_25_out,
       and_26_out, and_27_out, and_29_out, and_30_out, and_31_out, and_32_out, and_33_out, and_34_out,
       and_35_out, and_36_out, and_37_out, and_38_out, nand_2_out, nand_4_out, nor_2_out, nor_3_out,
       nor_4_out, nor_5_out, nor_6_out, nor_7_out, nor_8_out, nor_9_out, nor_10_out, nor_11_out, nor_12_out,
       not_1_out, not_2_out, not_3_out, not_4_out, not_5_out, not_6_out, not_7_out, not_8_out, not_9_out;

  and and_1 (and_1_out, nor_3_out, nor_3_out);
  and and_2 (and_2_out, nor_2_out, nor_6_out);
  nor nor_1 (G_, and_1_out, and_2_out, and_4_out, and_3_out, and_3_out);
  and and_3 (and_3_out, nor_2_out, nor_4_out, nor_8_out, nor_12_out, nor_12_out);
  and and_4 (and_4_out, nor_2_out, nor_4_out, nor_9_out);
  nor nor_2 (nor_2_out, and_5_out, and_6_out);
  and and_5 (and_5_out, B3_, S3, A3_);
  and and_6 (and_6_out, A3_, S2, not_1_out);
  nand nand_1 (Cn4, G_, nand_2_out);
  nand nand_2 (nand_2_out, nor_2_out, nor_4_out, nor_8_out, nor_11_out, Cn);
  and and_7 (and_7_out, not_1_out, S1);
  not not_1 (not_1_out, B3_);
  nand nand_3 (P_, nor_2_out, nor_4_out, nor_8_out, nor_11_out, nor_11_out);
  nor nor_3 (nor_3_out, and_7_out, and_8_out, and_9_out);
  and and_8 (and_8_out, S0, B3_);
  and and_9 (and_9_out, A3_, A3_);
  and and_10 (and_10_out, nor_2_out, not_2_out);
  not not_2 (not_2_out, nor_3_out);
  and and_11 (and_11_out, B2_, S3, A2_);
  xor xor_1 (F3_, and_10_out, nor_5_out);
  and and_12 (and_12_out, nor_4_out, nor_8_out, nor_12_out, not_9_out, not_9_out);
  and and_13 (and_13_out, nor_4_out, nor_8_out, nor_11_out, Cn, not_9_out);
  nor nor_4 (nor_4_out, and_11_out, and_14_out);
  and and_14 (and_14_out, A2_, S2, not_3_out);
  not not_3 (not_3_out, B2_);
  nor nor_5 (nor_5_out, and_13_out, and_12_out, and_16_out, and_15_out, and_15_out);
  and and_15 (and_15_out, nor_6_out, not_9_out);
  and and_16 (and_16_out, nor_4_out, nor_9_out, not_9_out);
  nor nor_6 (nor_6_out, and_17_out, and_18_out, and_20_out);
  and and_17 (and_17_out, not_3_out, S1);
  and and_18 (and_18_out, S0, B2_);
  and and_19 (and_19_out, nor_4_out, not_4_out);
  not not_4 (not_4_out, nor_6_out);
  and and_20 (and_20_out, A2_, A2_);
  xor xor_2 (F2_, and_19_out, nor_7_out);
  nor nor_7 (nor_7_out, and_21_out, and_22_out, and_25_out);
  and and_21 (and_21_out, nor_8_out, nor_8_out, nor_11_out, Cn, not_9_out);
  and and_22 (and_22_out, nor_8_out, nor_12_out, not_9_out);
  nor nor_8 (nor_8_out, and_23_out, and_24_out);
  and and_23 (and_23_out, B1_, S3, A1_);
  and and_24 (and_24_out, A1_, S2, not_5_out);
  and and_25 (and_25_out, nor_9_out, not_9_out);
  nor nor_9 (nor_9_out, and_27_out, and_26_out, and_30_out);
  and and_26 (and_26_out, S0, B1_);
  and and_27 (and_27_out, not_5_out, S1);
  not not_5 (not_5_out, B1_);
  and and_28 (A_B, F3_, F2_, F1_, F0_);
  and and_29 (and_29_out, nor_8_out, not_6_out);
  not not_6 (not_6_out, nor_9_out);
  and and_30 (and_30_out, A1_, A1_);
  xor xor_3 (F1_, and_29_out, nor_10_out);
  nor nor_10 (nor_10_out, and_31_out, and_34_out);
  and and_31 (and_31_out, Cn, nor_11_out, not_9_out);
  nor nor_11 (nor_11_out, and_33_out, and_32_out);
  and and_32 (and_32_out, A0_, S2, not_7_out);
  and and_33 (and_33_out, B0_, S3, A0_);
  and and_34 (and_34_out, nor_12_out, not_9_out);
  and and_35 (and_35_out, not_7_out, S1);
  not not_7 (not_7_out, B0_);
  and and_36 (and_36_out, nor_11_out, not_8_out);
  not not_8 (not_8_out, nor_12_out);
  nor nor_12 (nor_12_out, and_35_out, and_38_out, and_37_out);
  and and_37 (and_37_out, A0_, A0_);
  and and_38 (and_38_out, S0, B0_);
  xor xor_4 (F0_, and_36_out, nand_4_out);
  nand nand_4 (nand_4_out, not_9_out, Cn);
  not not_9 (not_9_out, M);
endmodule

module ic74xx182 (
  input  G0,
  input  P0,
  input  Cn,
  input  G1,
  input  P1,
  input  G2,
  input  P2,
  input  G3,
  input  P3,
  output CnX_,
  output CnY_,
  output CnZ_,
  output G,
  output P
);

  wire and_1_out, and_2_out, and_3_out, and_4_out, and_5_out, and_6_out, and_7_out, and_8_out, and_9_out,
       and_10_out, and_11_out, and_12_out, and_13_out, not_1_out;

  nor nor_1 (CnX_, and_1_out, and_2_out);
  and and_1 (and_1_out, G0, P0);
  and and_2 (and_2_out, G0, not_1_out);
  not not_1 (not_1_out, Cn);
  and and_3 (and_3_out, G1, P1);
  nor nor_2 (CnY_, and_3_out, and_4_out, and_5_out);
  and and_4 (and_4_out, G0, P0, G1);
  and and_5 (and_5_out, not_1_out, G0, G1);
  nor nor_3 (CnZ_, and_7_out, and_6_out, and_9_out, and_8_out);
  and and_6 (and_6_out, G1, P1, G2);
  and and_7 (and_7_out, G2, P2);
  and and_8 (and_8_out, not_1_out, not_1_out, G0, G1, G2);
  and and_9 (and_9_out, G0, G0, P0, G1, G2);
  or or_1 (G, and_11_out, and_10_out, and_12_out, and_13_out);
  and and_10 (and_10_out, G2, P2, G3);
  and and_11 (and_11_out, G3, P3);
  and and_12 (and_12_out, G1, G1, P1, G2, G3);
  or or_2 (P, P0, P1, P2, P3);
  and and_13 (and_13_out, G0, G0, G1, G2, G3);
endmodule

module ic74xx245 (
  input  DIR,
  input  EO_9639ac40,
  input  [7:0] AI,
  input  [7:0] BI,
  output [7:0] AO,
  output [7:0] BO
);

  wire and_1_out, and_2_out, not_1_out, not_2_out, not_3_out;

  not not_1 (not_1_out, EO_9639ac40);
  and and_1 (and_1_out, not_1_out, DIR);
  assign AO = and_1_out ? AI : 8'bz;  // Controlled_Buffer controlled_buffer_1
  not not_2 (not_2_out, DIR);
  not not_3 (not_3_out, EO_9639ac40);
  and and_2 (and_2_out, not_3_out, not_2_out);
  assign BO = and_2_out ? BI : 8'bz;  // Controlled_Buffer controlled_buffer_2
endmodule

module ic74xx273 (
  input  D0,
  input  D1,
  input  D2,
  input  D3,
  input  D4,
  input  D5,
  input  D6,
  input  D7,
  input  CP,
  input  MR_b7c3316e,
  output Q0,
  output Q1,
  output Q2,
  output Q3,
  output Q4,
  output Q5,
  output Q6,
  output Q7
);

  wire not_1_out;

  D_Flip_Flop d_ff_1 (.D(D0), .clk(CP), .Q(Q0), .reset(not_1_out));  // open: Qn, preset
  not not_1 (not_1_out, MR_b7c3316e);
  D_Flip_Flop d_ff_2 (.D(D1), .clk(CP), .Q(Q1), .reset(not_1_out));  // open: Qn, preset
  D_Flip_Flop d_ff_3 (.D(D2), .clk(CP), .Q(Q2), .reset(not_1_out));  // open: Qn, preset
  D_Flip_Flop d_ff_4 (.D(D3), .clk(CP), .Q(Q3), .reset(not_1_out));  // open: Qn, preset
  D_Flip_Flop d_ff_5 (.D(D4), .clk(CP), .Q(Q4), .reset(not_1_out));  // open: Qn, preset
  D_Flip_Flop d_ff_6 (.D(D5), .clk(CP), .Q(Q5), .reset(not_1_out));  // open: Qn, preset
  D_Flip_Flop d_ff_7 (.D(D6), .clk(CP), .Q(Q6), .reset(not_1_out));  // open: Qn, preset
  D_Flip_Flop d_ff_8 (.D(D7), .clk(CP), .Q(Q7), .reset(not_1_out));  // open: Qn, preset
endmodule

module ic74xx382 (
  input  Cn,
  input  B0,
  input  A0,
  input  B1,
  input  A1,
  input  B2,
  input  A2,
  input  B3,
  input  A3,
  input  S0,
  input  S1,
  input  S2,
  output F0,
  output F1,
  output F2,
  output F3,
  output OVR,
  output Cn_4
);

  wire and_1_out, and_2_out, and_3_out, and_4_out, and_5_out, and_6_out, and_7_out, and_8_out, and_9_out,
       and_10_out, and_11_out, and_12_out, and_13_out, and_14_out, and_15_out, and_16_out, and_17_out,
       and_18_out, and_19_out, and_20_out, and_21_out, and_22_out, and_23_out, and_24_out, and_25_out,
       and_26_out, and_27_out, and_28_out, and_29_out, and_30_out, and_31_out, and_32_out, and_33_out,
       and_34_out, and_35_out, and_36_out, and_37_out, and_38_out, and_39_out, and_40_out, and_41_out,
       and_42_out, and_43_out, and_44_out, and_45_out, nand_1_out, nand_2_out, nand_3_out, nand_4_out,
       nand_6_out, nand_7_out, nor_1_out, nor_2_out, nor_3_out, nor_4_out, nor_5_out, nor_6_out, nor_7_out,
       nor_8_out, nor_9_out, nor_10_out, nor_11_out, nor_12_out, nor_13_out, nor_14_out, not_1_out,
       not_2_out, not_3_out, not_4_out, not_5_out, not_6_out, not_7_out, not_8_out, not_9_out, not_10_out,
       not_11_out, not_12_out, not_13_out, not_14_out;

  and and_1 (and_1_out, not_2_out, not_2_out, not_1_out, nand_3_out, nand_7_out);
  nor nor_1 (nor_1_out, and_1_out, and_2_out, and_4_out);
  and and_2 (and_2_out, nand_4_out, nand_3_out, nand_2_out, not_1_out, A0);
  not not_1 (not_1_out, B0);
  and and_3 (and_3_out, not_2_out, not_1_out, nand_4_out, nand_2_out, nor_14_out);
  and and_4 (and_4_out, nand_7_out, nand_7_out, nand_2_out, B0, not_2_out);
  xor xor_1 (F0, nand_1_out, nor_2_out);
  nand nand_1 (nand_1_out, Cn, nor_12_out);
  nor nor_2 (nor_2_out, and_3_out, and_3_out, and_5_out, and_6_out, and_7_out);
  and and_5 (and_5_out, nand_7_out, nand_7_out, nand_3_out, not_1_out, A0);
  not not_2 (not_2_out, A0);
  and and_6 (and_6_out, nand_7_out, nand_7_out, nand_3_out, B0, not_2_out);
  and and_7 (and_7_out, nand_4_out, nand_4_out, nand_2_out, B0, A0);
  and and_8 (and_8_out, not_4_out, not_4_out, not_3_out, nand_3_out, nand_7_out);
  not not_3 (not_3_out, B1);
  nor nor_3 (nor_3_out, and_8_out, and_9_out, and_10_out);
  and and_9 (and_9_out, nand_4_out, nand_3_out, nand_2_out, not_3_out, A1);
  and and_10 (and_10_out, nand_7_out, nand_7_out, nand_2_out, B1, not_4_out);
  and and_11 (and_11_out, Cn, nor_1_out, nor_12_out);
  and and_12 (and_12_out, not_4_out, not_3_out, nand_4_out, nand_2_out, nor_14_out);
  xor xor_2 (F1, nor_4_out, nor_5_out);
  nor nor_4 (nor_4_out, and_11_out, and_13_out);
  and and_13 (and_13_out, nor_1_out, nor_2_out, nor_12_out);
  nor nor_5 (nor_5_out, and_12_out, and_12_out, and_14_out, and_15_out, and_16_out);
  and and_14 (and_14_out, nand_7_out, nand_7_out, nand_3_out, not_3_out, A1);
  not not_4 (not_4_out, A1);
  and and_15 (and_15_out, nand_7_out, nand_7_out, nand_3_out, B1, not_4_out);
  and and_16 (and_16_out, nand_4_out, nand_4_out, nand_2_out, B1, A1);
  nor nor_6 (nor_6_out, and_17_out, and_18_out, and_20_out);
  and and_17 (and_17_out, not_6_out, not_6_out, not_5_out, nand_3_out, nand_7_out);
  and and_18 (and_18_out, nand_4_out, nand_3_out, nand_2_out, not_5_out, A2);
  not not_5 (not_5_out, B2);
  and and_19 (and_19_out, Cn, Cn, nor_1_out, nor_3_out, nor_12_out);
  and and_20 (and_20_out, nand_7_out, nand_7_out, nand_2_out, B2, not_6_out);
  nor nor_7 (nor_7_out, and_19_out, and_21_out, and_23_out);
  and and_21 (and_21_out, nor_1_out, nor_1_out, nor_3_out, nor_2_out, nor_12_out);
  and and_22 (and_22_out, not_6_out, not_5_out, nand_4_out, nand_2_out, nor_14_out);
  not not_6 (not_6_out, A2);
  xor xor_3 (F2, nor_7_out, nor_8_out);
  and and_23 (and_23_out, nor_3_out, nor_5_out, nor_12_out);
  nor nor_8 (nor_8_out, and_22_out, and_22_out, and_25_out, and_24_out, and_26_out);
  and and_24 (and_24_out, nand_7_out, nand_7_out, nand_3_out, B2, not_6_out);
  and and_25 (and_25_out, nand_7_out, nand_7_out, nand_3_out, not_5_out, A2);
  and and_26 (and_26_out, nand_4_out, nand_4_out, nand_2_out, B2, A2);
  and and_27 (and_27_out, not_8_out, not_8_out, not_7_out, nand_3_out, nand_7_out);
  and and_28 (and_28_out, Cn, nor_1_out, nor_3_out, nor_6_out, nor_12_out);
  and and_29 (and_29_out, nor_1_out, nor_3_out, nor_6_out, nor_2_out, nor_12_out);
  nor nor_9 (nor_9_out, and_27_out, and_30_out, and_32_out);
  and and_30 (and_30_out, nand_4_out, nand_3_out, nand_2_out, not_7_out, A3);
  not not_7 (not_7_out, B3);
  nor nor_10 (nor_10_out, and_28_out, and_28_out, and_29_out, and_31_out, and_33_out);
  and and_31 (and_31_out, nor_3_out, nor_3_out, nor_6_out, nor_5_out, nor_12_out);
  and and_32 (and_32_out, nand_7_out, nand_7_out, nand_2_out, B3, not_8_out);
  and and_33 (and_33_out, nor_6_out, nor_8_out, nor_12_out);
  and and_34 (and_34_out, not_8_out, not_7_out, nand_4_out, nand_2_out, nor_14_out);
  and and_35 (and_35_out, nand_7_out, nand_7_out, nand_3_out, not_7_out, A3);
  not not_8 (not_8_out, A3);
  xor xor_4 (F3, nor_10_out, nor_11_out);
  nor nor_11 (nor_11_out, and_34_out, and_34_out, and_35_out, and_36_out, and_38_out);
  and and_36 (and_36_out, nand_7_out, nand_7_out, nand_3_out, B3, not_8_out);
  and and_37 (and_37_out, nor_1_out, nor_3_out, nor_6_out, nor_9_out, nor_2_out);
  nor nor_12 (nor_12_out, not_13_out, and_40_out);
  and and_38 (and_38_out, nand_4_out, nand_4_out, nand_2_out, B3, A3);
  nor nor_13 (nor_13_out, and_37_out, and_37_out, and_39_out, and_42_out, and_43_out);
  and and_39 (and_39_out, nor_3_out, nor_3_out, nor_6_out, nor_9_out, nor_5_out);
  and and_40 (and_40_out, not_10_out, not_11_out);
  xor xor_5 (OVR, nor_10_out, and_41_out);
  and and_41 (and_41_out, nor_13_out, nand_6_out);
  and and_42 (and_42_out, nor_6_out, nor_9_out, nor_8_out);
  and and_43 (and_43_out, nor_9_out, nor_11_out);
  and and_44 (and_44_out, not_10_out, not_13_out);
  nand nand_2 (nand_2_out, not_9_out, not_12_out, not_14_out);
  nand nand_3 (nand_3_out, not_10_out, not_12_out);
  nand nand_4 (nand_4_out, not_10_out, not_11_out);
  not not_9 (not_9_out, not_10_out);
  not not_10 (not_10_out, S0);
  nand nand_5 (Cn_4, nor_13_out, nand_6_out);
  nand nand_6 (nand_6_out, Cn, nor_1_out, nor_3_out, nor_6_out, nor_9_out);
  nor nor_14 (nor_14_out, and_44_out, and_45_out);
  and and_45 (and_45_out, not_11_out, not_13_out);
  nand nand_7 (nand_7_out, not_11_out, not_14_out);
  not not_11 (not_11_out, S1);
  not not_12 (not_12_out, not_11_out);
  not not_13 (not_13_out, not_14_out);
  not not_14 (not_14_out, S2);
endmodule

module testParts (
  input  OutEn,
  input  in_2,
  input  in_3,
  input  in_4,
  input  [3:0] Number_A,
  input  [3:0] Number_B,
  input  in_7,
  input  [3:0] in_8,
  input  in_9,
  input  DataEn,
  input  Cn,
  input  [11:0] in_12,
  input  in_13,
  input  in_14,
  input  [2:0] Fn_Select,
  input  in_16,
  input  in_17,
  input  in_18,
  input  in_19,
  input  in_20,
  input  in_21,
  input  in_22,
  input  in_23,
  input  in_24,
  input  in_25,
  input  Func_Select,
  input  [11:0] in_27,
  input  in_28,
  input  in_29,
  input  in_30,
  input  [15:0] Reg_A,
  input  [11:0] in_32,
  input  in_33,
  input  in_34,
  input  in_35,
  input  [15:0] in_36,
  input  in_37,
  input  [15:0] Reg_B,
  input  in_39,
  input  in_40,
  input  [15:0] in_41,
  input  [3:0] in_42,
  input  in_43,
  input  in_44,
  input  in_45,
  output [3:0] out_46,
  output [11:0] out_47,
  output out_48,
  output Overflow,
  output [4:0] Function_Output,
  output out_51,
  output out_52,
  output [15:0] out_53
);

  wire button_1_out, button_2_out, CLK, CLK_0416f44f, partalu_1_cf_led, partalu_1_overflow, partalu_1_zf_led,
       partclk_1_led, partctrl_1_ai_f325b2de, partctrl_1_an, partctrl_1_ao_fda11864, partctrl_1_bi_dc5a9e0c,
       partctrl_1_ce, partctrl_1_clr, partctrl_1_clr_87b95d37, partctrl_1_co_e8fa446c,
       partctrl_1_eo_bf3b4110, partctrl_1_fi_fa84cb50, partctrl_1_hlt, partctrl_1_ii_51e65cc3,
       partctrl_1_io_06df68e4, partctrl_1_j_e6dac3f4, partctrl_1_mi_1a8064a7, partctrl_1_nt, partctrl_1_oi,
       partctrl_1_r, partctrl_1_ri, partctrl_1_ro_f7a11c4b, partctrl_1_su, partctrl_1_xr, partmar_1_prog,
       partmar_1_progled, partmar_1_runled;
  wire [2:0] partctrl_1_count_leds;
  wire [4:0] partctrl_1_time_leds_backwards;
  wire [11:0] partmar_1_a;
  wire [15:0] partalu_1_buso, partreg_1_rego, partreg_2_rego;

  partCLK partclk_1 (
    .CLK(CLK), .Mode(1'b1), .HLT(1'b0), .CLK_7d3332a1(CLK_0416f44f), .LED(partclk_1_led));  // open: Pulse
  LED led_1 (.in(partclk_1_led));
  // Probe on Reg_A
  // Probe on partalu_1_buso
  // Probe on Reg_B
  // Probe on Reg_A
  // Probe on partalu_1_buso
  // Probe on partalu_1_buso
  // Probe on Reg_B
  Button button_1 (.out(button_1_out));
  // Probe on partctrl_1_count_leds
  // Probe on partctrl_1_time_leds_backwards
  partREG partreg_1 (
    .RegO(partreg_1_rego), .CLK(CLK), .CLR(in_18), .xI_9c528b91(in_16), .xO_05de6390(in_17), .BusI(Reg_A));  // open: BusO, LEDs
  partREG partreg_2 (
    .RegO(partreg_2_rego), .CLK(CLK), .CLR(in_40), .xI_9c528b91(in_35), .xO_05de6390(in_39), .BusI(Reg_B));  // open: BusO, LEDs
  partCTRL partctrl_1 (
    .CLR(partctrl_1_clr), .MI_1a8064a7(partctrl_1_mi_1a8064a7), .CFI(in_43),
    .AI_f325b2de(partctrl_1_ai_f325b2de), .J_e6dac3f4(partctrl_1_j_e6dac3f4),
    .CLR_87b95d37(partctrl_1_clr_87b95d37), .II_51e65cc3(partctrl_1_ii_51e65cc3), .RegI(in_42),
    .RI(partctrl_1_ri), .CE(partctrl_1_ce), .HLT(partctrl_1_hlt), .ZFI(in_44),
    .AO_fda11864(partctrl_1_ao_fda11864), .FI_fa84cb50(partctrl_1_fi_fa84cb50),
    .Time_LEDs_backwards(partctrl_1_time_leds_backwards), .IO_06df68e4(partctrl_1_io_06df68e4),
    .CLK_0416f44f(button_1_out), .RO_f7a11c4b(partctrl_1_ro_f7a11c4b), .CO_e8fa446c(partctrl_1_co_e8fa446c),
    .Count_LEDs(partctrl_1_count_leds), .Reset(in_45), .OI(partctrl_1_oi),
    .BI_dc5a9e0c(partctrl_1_bi_dc5a9e0c), .SU(partctrl_1_su), .EO_bf3b4110(partctrl_1_eo_bf3b4110),
    .NT(partctrl_1_nt), .AN(partctrl_1_an), .R(partctrl_1_r), .XR(partctrl_1_xr));  // open: CTRL_LEDs
  ic74xx173 ic74xx173_1 (
    .CLR(in_2), .N_edc11205(in_7), .G2_ba7b7058(DataEn), .D(in_8), .M_5f199db6(OutEn), .CLK(CLK),
    .G1_eeaaf593(in_14), .Q(out_46));
  partALU partalu_1 (
    .BusO(partalu_1_buso), .A(partreg_1_rego), .EO_a0c37f53(in_19), .NT(in_29), .B(partreg_2_rego),
    .SU(in_20), .AN(in_28), .CLK(CLK), .CLR(in_25), .XR(in_24), .R(Func_Select), .FI_261165dc(in_21),
    .Overflow(partalu_1_overflow), .CF_LED(partalu_1_cf_led), .ZF_LED(partalu_1_zf_led), .CF(out_51),
    .ZF(out_52));  // open: RES_LEDs
  LED led_2 (.in(partalu_1_overflow));
  LED led_3 (.in(partalu_1_cf_led));
  LED led_4 (.in(partalu_1_zf_led));
  L_74382_7733abc4 l_74382_7733abc4_1 (
    .Cn(Cn), .B0(Number_B[0]), .A0(Number_A[0]), .B1(Number_B[1]), .A1(Number_A[1]), .B2(Number_B[2]),
    .A2(Number_A[2]), .B3(Number_B[3]), .A3(Number_A[3]), .S0(Fn_Select[0]), .S1(Fn_Select[1]),
    .S2(Fn_Select[2]), .F0(Function_Output[0]), .F1(Function_Output[1]), .F2(Function_Output[2]),
    .F3(Function_Output[3]), .OVR(Overflow), .Cn_4_58451dc4(Function_Output[4]));
  // Probe on partmar_1_a
  Button button_2 (.out(button_2_out));
  partMAR partmar_1 (
    .RunLED(partmar_1_runled), .AddrSWs_d391c16e(in_32), .CLR(in_23), .Mode(in_30), .CLK(CLK), .BusI(in_27),
    .MI_85f63c41(in_22), .A(partmar_1_a), .ProgLED(partmar_1_progled), .PROG(partmar_1_prog));  // open: A_LEDs
  LED led_5 (.in(partmar_1_runled));
  LED led_6 (.in(partmar_1_progled));
  partRAM partram_1 (
    .ProgOK(button_2_out), .RI(in_34), .A(partmar_1_a), .ProgSW(in_41), .BusI(in_36), .CLK(CLK),
    .RO_b3172779(in_37), .PROG(partmar_1_prog), .BusO(out_53), .CLR(in_33));  // open: LEDs
  partPC partpc_1 (
    .BusO(out_47), .CLK(CLK), .CLR_b6b4cc54(in_13), .CE(in_3), .BusI(in_12), .CO_d457f91e(in_4),
    .J_ab0d5ac6(in_9), .TerminalCount(out_48));  // open: LEDs
  // also tied to GND on the sheet: {partctrl_1_hlt, partctrl_1_ri, partctrl_1_su, partctrl_1_oi, partctrl_1_ce, partctrl_1_xr, partctrl_1_r, partctrl_1_an, partctrl_1_nt}
  // also tied to VCC on the sheet: {partctrl_1_mi_1a8064a7, partctrl_1_ro_f7a11c4b, partctrl_1_io_06df68e4, partctrl_1_ii_51e65cc3, partctrl_1_ai_f325b2de, partctrl_1_ao_fda11864, partctrl_1_eo_bf3b4110, partctrl_1_bi_dc5a9e0c, partctrl_1_co_e8fa446c, partctrl_1_j_e6dac3f4, partctrl_1_fi_fa84cb50}

  // Notes on the sheet:
  //   Func Out
endmodule

module testMain (
  input  in_1,
  input  [11:0] in_2,
  input  in_3,
  input  [15:0] in_4,
  input  in_5,
  input  in_6,
  output [15:0] out_7,
  output [11:0] out_8,
  output [2:0] out_9
);

  wire maininternal_1_p3, maininternal_1_p4;

  Button button_1 ();  // open: out
  Button button_2 ();  // open: out
  Button button_3 ();  // open: out
  _7_Segment_Display u_7_segment_display_1 ();  // open: g, f, a, b, e, d, c, dp
  _7_Segment_Display u_7_segment_display_2 ();  // open: g, f, a, b, e, d, c, dp
  _7_Segment_Display u_7_segment_display_3 ();  // open: g, f, a, b, e, d, c, dp
  _7_Segment_Display u_7_segment_display_4 ();  // open: g, f, a, b, e, d, c, dp
  // mainInternal maininternal_1: pin names not known; wires that end beside it: out_7, out_8, maininternal_1_p3, maininternal_1_p4
  LED led_1 ();  // open: in
  LED led_2 (.in(maininternal_1_p3));
  LED led_3 ();  // open: in
  LED led_4 ();  // open: in
  LED led_5 (.in(maininternal_1_p4));
endmodule

module oldPartALU (
  input  in_1,
  input  in_2,
  input  in_3,
  input  in_4,
  input  in_5,
  input  in_6,
  input  [15:0] in_7,
  input  [15:0] in_8,
  input  in_9,
  input  in_10,
  input  in_11,
  output [15:0] out_12,
  output [15:0] out_13,
  output out_14,
  output out_15,
  output out_16,
  output out_17,
  output out_18
);

  wire nand_1_out, nor_1_out, not_1_out, not_2_out, or_2_out;
  wire [2:0] or_1_out;
  wire [3:0] sub16bitalu_1_p6;
  wire [3:2] ic74xx173_1_q;
  wire [7:0] pull_resistor_1_node, pull_resistor_1_node_2;
  wire [15:0] not_3_out, sub16bitalu_1_p7;

  nor nor_1 (nor_1_out, in_5, in_4, in_3, in_2, in_6);
  or or_1 (or_1_out[0], nor_1_out, in_4);
  not not_1 (not_1_out, in_5);
  nand nand_1 (nand_1_out, not_1_out, or_2_out);
  or or_2 (or_2_out, in_3, in_4);
  or or_3 (or_1_out[2], in_3, in_5, in_4);
  xor xor_1 (or_1_out[1], in_6, nand_1_out);
  not not_2 (not_2_out, in_6);
  ic74xx245 ic74xx245_1 (.EO_9639ac40(in_1), .BI(out_12[7:0]), .DIR(1'b0), .BO(out_13[7:0]));  // open: AO, AI
  ic74xx245 ic74xx245_2 (.EO_9639ac40(in_1), .BI(out_12[15:8]), .DIR(1'b0), .BO(out_13[15:8]));  // open: AO, AI
  assign not_3_out = ~in_7;  // NOT_Gate not_3, 16 bits wide
  // sub16bitALU sub16bitalu_1: pin names not known; wires that end beside it: in_7, in_8, in_2, or_1_out, out_14, sub16bitalu_1_p6[0], sub16bitalu_1_p7
  assign out_12 = sub16bitalu_1_p7 | {pull_resistor_1_node_2, pull_resistor_1_node};  // OR_Gate or_4, 16 bits wide
  Pull_Resistor pull_resistor_1 (.node({pull_resistor_1_node_2, pull_resistor_1_node}));
  ic74xx245 ic74xx245_3 (
    .EO_9639ac40(not_2_out), .AO(pull_resistor_1_node), .DIR(1'b1), .AI(not_3_out[7:0]));  // open: BI, BO
  ic74xx245 ic74xx245_4 (
    .EO_9639ac40(not_2_out), .AO(pull_resistor_1_node_2), .DIR(1'b1), .AI(not_3_out[15:8]));  // open: BI, BO
  ic74xx173 ic74xx173_1 (
    .CLR(in_9), .N_edc11205(1'b0), .G2_ba7b7058(in_10), .D(sub16bitalu_1_p6), .M_5f199db6(1'b0), .CLK(in_11),
    .G1_eeaaf593(in_10), .Q({ic74xx173_1_q, out_16, out_15}));
  nor nor_2 (sub16bitalu_1_p6[1], out_12[0], out_12[1], out_12[2], out_12[3], out_12[4], out_12[5], out_12[6], out_12[7], out_12[9], out_12[10], out_12[11], out_12[12], out_12[13], out_12[14], out_12[15], out_12[8]);

  assign out_17 = out_15;
  assign out_18 = out_16;

  // Notes on the sheet:
  //   ZERO Flag
endmodule

module oldSub16bitALU (
  input  [15:0] in_1,
  input  [15:0] in_2,
  input  in_3,
  input  [2:0] in_4,
  input  [15:0] in_5,
  input  [15:0] in_6,
  input  in_7,
  input  in_8,
  input  [3:0] in_9,
  output out_10,
  output out_11,
  output [15:0] out_12,
  output out_13,
  output out_14,
  output [15:0] out_15
);

  wire ic74xx181_2_cn4, ic74xx181_3_cn4, ic74xx181_4_p13, ic74xx181_4_p21, ic74xx382_1_cn_4,
       ic74xx382_2_cn_4, ic74xx382_3_cn_4;

  // Probe on in_1
  // Probe on in_1
  ic74xx382 ic74xx382_1 (
    .F0(out_12[0]), .A2(in_1[2]), .Cn(in_3), .B2(in_2[2]), .S2(in_4[2]), .B3(in_2[3]), .B0(in_2[0]),
    .A1(in_1[1]), .S1(in_4[1]), .A3(in_1[3]), .A0(in_1[0]), .B1(in_2[1]), .S0(in_4[0]), .F1(out_12[1]),
    .F2(out_12[2]), .F3(out_12[3]), .Cn_4(ic74xx382_1_cn_4));  // open: OVR
  ic74xx181 ic74xx181_1 (
    .Cn4(out_13), .Cn(ic74xx181_2_cn4), .M(in_7), .A0_(in_5[0]), .B0_(in_6[0]), .A1_(in_5[1]), .B1_(in_6[1]),
    .A2_(in_5[2]), .B2_(in_6[2]), .A3_(in_5[3]), .B3_(in_6[3]), .S0(in_9[0]), .S1(in_9[1]), .S2(in_9[2]),
    .S3(in_9[3]), .F3_(out_15[3]), .F2_(out_15[2]), .A_B(out_14), .F1_(out_15[1]), .F0_(out_15[0]));  // open: G_, P_
  // Probe on in_5
  // Probe on in_2
  ic74xx382 ic74xx382_2 (
    .F0(out_12[4]), .A2(in_1[6]), .Cn(ic74xx382_1_cn_4), .B2(in_2[6]), .S2(in_4[2]), .B3(in_2[7]),
    .B0(in_2[4]), .A1(in_1[5]), .S1(in_4[1]), .A3(in_1[7]), .A0(in_1[4]), .B1(in_2[5]), .S0(in_4[0]),
    .F1(out_12[5]), .F2(out_12[6]), .F3(out_12[7]), .Cn_4(ic74xx382_2_cn_4));  // open: OVR
  // Probe on out_12
  // Probe on out_12
  // Probe on in_5
  ic74xx181 ic74xx181_2 (
    .Cn4(ic74xx181_2_cn4), .Cn(ic74xx181_3_cn4), .M(in_7), .A0_(in_5[4]), .B0_(in_6[4]), .A1_(in_5[5]),
    .B1_(in_6[5]), .A2_(in_5[6]), .B2_(in_6[6]), .A3_(in_5[7]), .B3_(in_6[7]), .S0(in_9[0]), .S1(in_9[1]),
    .S2(in_9[2]), .S3(in_9[3]), .F3_(out_15[7]), .F2_(out_15[6]), .A_B(out_14), .F1_(out_15[5]),
    .F0_(out_15[4]));  // open: G_, P_
  // Probe on in_2
  // Probe on out_15
  ic74xx382 ic74xx382_3 (
    .F0(out_12[8]), .A2(in_1[10]), .Cn(ic74xx382_2_cn_4), .B2(in_2[10]), .S2(in_4[2]), .B3(in_2[11]),
    .B0(in_2[8]), .A1(in_1[9]), .S1(in_4[1]), .A3(in_1[11]), .A0(in_1[8]), .B1(in_2[9]), .S0(in_4[0]),
    .F1(out_12[9]), .F2(out_12[10]), .F3(out_12[11]), .Cn_4(ic74xx382_3_cn_4));  // open: OVR
  ic74xx181 ic74xx181_3 (
    .Cn4(ic74xx181_3_cn4), .Cn(ic74xx181_4_p21), .M(in_7), .A0_(in_5[8]), .B0_(in_6[8]), .A1_(in_5[9]),
    .B1_(in_6[9]), .A2_(in_5[10]), .B2_(in_6[10]), .A3_(in_5[11]), .B3_(in_6[11]), .S0(in_9[0]),
    .S1(in_9[1]), .S2(in_9[2]), .S3(in_9[3]), .F3_(out_15[11]), .F2_(out_15[10]), .A_B(out_14),
    .F1_(out_15[9]), .F0_(out_15[8]));  // open: G_, P_
  // Probe on out_15
  // Probe on in_6
  // Probe on in_6
  ic74xx382 ic74xx382_4 (
    .F0(out_12[12]), .A2(in_1[14]), .Cn(ic74xx382_3_cn_4), .B2(in_2[14]), .S2(in_4[2]), .B3(in_2[15]),
    .B0(in_2[12]), .A1(in_1[13]), .S1(in_4[1]), .A3(in_1[15]), .A0(in_1[12]), .B1(in_2[13]), .S0(in_4[0]),
    .F1(out_12[13]), .F2(out_12[14]), .F3(out_12[15]), .OVR(out_11), .Cn_4(out_10));
  // ic74xx181 ic74xx181_4: pin names not known; wires that end beside it: in_5[12], in_5[13], in_5[14], in_5[15], in_6[12], in_6[13], in_6[14], in_6[15], in_9[0], in_9[1], in_9[2], in_9[3], ic74xx181_4_p13, ic74xx181_4_p13, in_7, in_8, out_15[12], out_15[13], out_15[14], out_15[15], ic74xx181_4_p21, out_14
endmodule
