// Logisim project Abacus_PCB.circ as structural Verilog
module subClock (
  input  Mode,
  input  Pulse,
  input  Hlt,
  output LedClk,
  output Clk,
  output _Clk
);

  wire and_1_out, and_2_out, clock_1_out, not_1_out, not_2_out, or_1_out;

  Clock clock_1 (.out(clock_1_out));
  not not_1 (not_1_out, Mode);
  and and_1 (and_1_out, clock_1_out, Mode);
  or or_1 (or_1_out, and_1_out, and_2_out);
  and and_2 (and_2_out, not_1_out, Pulse);
  not not_2 (not_2_out, Hlt);
  and and_3 (Clk, or_1_out, not_2_out);
  not not_3 (_Clk, Clk);

  assign LedClk = Clk;
endmodule

module subPC (
  input  Jc,
  input  Fc,
  input  J,
  input  Jz,
  input  Fz,
  input  Co,
  input  in_7,
  input  in_8,
  input  in_9,
  input  in_10,
  input  in_11,
  input  in_12,
  input  in_13,
  input  in_14,
  input  in_15,
  input  in_16,
  input  in_17,
  input  in_18,
  input  _Clr,
  input  Clk,
  input  Ce,
  output Tc,
  output out_23,
  output out_24,
  output out_25,
  output out_26,
  output out_27,
  output out_28,
  output out_29,
  output out_30,
  output out_31,
  output out_32,
  output out_33,
  output out_34,
  output out_35,
  output out_36,
  output out_37,
  output out_38,
  output out_39,
  output out_40,
  output out_41,
  output out_42,
  output out_43,
  output out_44,
  output out_45,
  output out_46
);

  wire ic245_1_out_19, ic245_1_out_20, ic245_1_out_21, ic245_1_out_22, ic245_1_out_23, ic245_1_out_24,
       ic245_1_out_25, ic245_1_out_27, ic245_1_out_29, ic245_1_out_31, ic245_1_out_33, ic245_1_out_34,
       ic245_2_out_21, ic245_2_out_23, ic245_2_out_25, ic245_2_out_27, ic245_2_out_29, ic245_2_out_31,
       ic245_2_out_33, ic245_2_out_34, n7408_1_p3, n7408_1_p6, n7432_1_p3, n74161_2_p3, n74161_2_p5,
       n74161_3_p3;

  // _7408 7408_1: pin names not known; wires that end beside it: Jc, Fc, n7408_1_p3, Jz, Fz, n7408_1_p6
  ic245 ic245_1 (
    .out_19(ic245_1_out_19), .out_20(ic245_1_out_20), .out_21(ic245_1_out_21), .out_22(ic245_1_out_22),
    .out_23(ic245_1_out_23), .out_24(ic245_1_out_24), .out_25(ic245_1_out_25), .out_26(out_23),
    .out_27(ic245_1_out_27), .out_28(out_24), .out_29(ic245_1_out_29), .out_30(out_25),
    .out_31(ic245_1_out_31), .out_32(out_26), .out_33(ic245_1_out_33), .out_34(ic245_1_out_34),
    .in_3(ic245_1_out_19), .in_4(ic245_1_out_20), .in_5(ic245_1_out_21), .in_6(ic245_1_out_22),
    .in_7(ic245_1_out_23), .in_8(ic245_1_out_24), .in_9(ic245_1_out_25), .in_10(out_23),
    .in_11(ic245_1_out_27), .in_12(out_24), .in_13(ic245_1_out_29), .in_14(out_25), .in_15(ic245_1_out_31),
    .in_16(out_26), .in_17(ic245_1_out_33), .in_18(ic245_1_out_34), .in_1(1'b1), .in_2(Co));
  ic245 ic245_2 (
    .out_19(out_27), .out_20(out_28), .out_21(ic245_2_out_21), .out_22(out_29), .out_23(ic245_2_out_23),
    .out_24(out_30), .out_25(ic245_2_out_25), .out_26(out_31), .out_27(ic245_2_out_27), .out_28(out_32),
    .out_29(ic245_2_out_29), .out_30(out_33), .out_31(ic245_2_out_31), .out_32(out_34),
    .out_33(ic245_2_out_33), .out_34(ic245_2_out_34), .in_3(out_27), .in_4(out_28), .in_5(ic245_2_out_21),
    .in_6(out_29), .in_7(ic245_2_out_23), .in_8(out_30), .in_9(ic245_2_out_25), .in_10(out_31),
    .in_11(ic245_2_out_27), .in_12(out_32), .in_13(ic245_2_out_29), .in_14(out_33), .in_15(ic245_2_out_31),
    .in_16(out_34), .in_17(ic245_2_out_33), .in_18(ic245_2_out_34), .in_1(1'b1), .in_2(Co));
  // _74161 74161_1: pin names not known; wires that end beside it: Tc, Clk, ic245_2_out_34, in_7, ic245_2_out_33, in_8, ic245_2_out_31, in_9
  // _74161 74161_2: pin names not known; wires that end beside it: ic245_2_out_29, in_10, n74161_2_p3, Ce, n74161_2_p5, _Clr, n74161_2_p3, Clk, ic245_2_out_27, in_11, ic245_2_out_25, in_12, ic245_2_out_23, in_13
  // _74161 74161_3: pin names not known; wires that end beside it: ic245_2_out_21, in_14, n74161_3_p3, Ce, n74161_2_p5, _Clr, n74161_3_p3, Clk, ic245_1_out_34, in_15, ic245_1_out_33, in_16, ic245_1_out_31, in_17, ic245_1_out_29, in_18, Ce, Ce, n74161_2_p5
  // _7432 7432_1: pin names not known; wires that end beside it: n7408_1_p3, n7408_1_p6, n7432_1_p3, n7432_1_p3, J, n74161_2_p5

  assign out_35 = out_23;
  assign out_36 = out_24;
  assign out_37 = out_25;
  assign out_38 = out_26;
  assign out_39 = out_27;
  assign out_40 = out_28;
  assign out_41 = out_29;
  assign out_42 = out_30;
  assign out_43 = out_31;
  assign out_44 = out_32;
  assign out_45 = out_33;
  assign out_46 = out_34;
endmodule
