// Logisim project Abacus_Revised.circ as structural Verilog
module main (
  input  [11:0] in_1,
  input  in_2,
  input  in_3,
  input  [15:0] in_4
);

  wire Ai, An, Ao, Bi, Ce, Clk, ClkInv, Co, Eo, Fc, Fi, Fo, Fz, Hlt, Ii, Io, J, Jc, Jz, Mi, MstRst, Nt, Oi,
       Ore, Prog, Pulse, Ri, Ro, Rst, Su, Xr;
  wire [2:0] control_1_t;
  wire [3:0] alu_1_flags, display_1_dispout, display_1_dispout_2, hex_digit_display_2_p1,
       hex_digit_display_3_p1, instr_1_regout;
  wire [11:0] mar_1_addr, pc_1_busout;
  wire [15:0] A_q, B_q;
  wire [15:12] memory_1_busout;

  Button button_1 (.out(MstRst));
  Button button_2 (.out(Pulse));
  clocks clocks_1 (.ClkInv(ClkInv), .ClkMode(in_2), .Clk(Clk), .Hlt(Hlt), .ClkPulse(Pulse));
  pc pc_1 (
    .Co(Co), .Fz(Fz), .Jc(Jc), .Jz(Jz), .Clk(Clk), .J(J), .Fc(Fc), .Rst(Rst), .Ce(Ce), .BusIn(pc_1_busout),
    .BusOut(pc_1_busout));
  mar mar_1 (.Clk(Clk), .ProgIn(in_1), .Mode(in_3), .BusIn(pc_1_busout), .Mi(Mi), .Clr(Rst), .Addr(mar_1_addr));
  // Probe on mar_1_addr
  memory memory_1 (
    .BusIn({memory_1_busout, pc_1_busout}), .Ro(Ro), .Prog(Prog), .Addr(mar_1_addr), .Mode(in_3), .Ri(Ri),
    .Clk(Clk), .ProgIn(in_4), .BusOut({memory_1_busout, pc_1_busout}));
  Register #(.width(16)) A (.D({memory_1_busout, pc_1_busout}), .en(Ai), .clk(Clk), .Q(A_q), .clr(Rst));
  Pull_Resistor pull_resistor_1 (.node({memory_1_busout, pc_1_busout}));
  Register #(.width(16)) B (.D({memory_1_busout, pc_1_busout}), .en(Bi), .clk(Clk), .Q(B_q), .clr(Rst));
  // Probe on {memory_1_busout, pc_1_busout}
  Button button_3 (.out(Prog));
  assign {memory_1_busout, pc_1_busout} = Ao ? A_q : 16'bz;  // Controlled_Buffer controlled_buffer_1
  alu alu_1 (
    .Nt(Nt), .An(An), .Su(Su), .AIn(A_q), .BIn(B_q), .Xr(Xr), .Ore(Ore),
    .BusOut({memory_1_busout, pc_1_busout}), .Eo(Eo), .Flags(alu_1_flags));
  Hex_Digit_Display hex_digit_display_1 (.value(display_1_dispout_2));  // open: dp
  // Probe on control_1_t
  // Hex_Digit_Display hex_digit_display_2: pin names not known; wires that end beside it: hex_digit_display_2_p1
  // Hex_Digit_Display hex_digit_display_3: pin names not known; wires that end beside it: hex_digit_display_3_p1
  display display_1 (
    .DispOut({display_1_dispout_2, hex_digit_display_2_p1, hex_digit_display_3_p1, display_1_dispout}),
    .Clk(Clk), .BusIn({memory_1_busout, pc_1_busout}), .Oi(Oi), .Clr(Rst));
  flags flags_1 (
    .Fi(Fi), .Fo(Fo), .Clk(Clk), .Rst(Rst), .BusOut(pc_1_busout[3:0]), .Flags(alu_1_flags), .FzO(Fz), .FcO(Fc));
  control control_1 (
    .Rst(Rst), .RegIn(instr_1_regout),
    .Ctrls({Jz, Jc, Fo, Nt, Ore, An, Xr, Fi, J, Co, Ce, Oi, Bi, Su, Eo, Ao, Ai, Ii, Io, Ro, Ri, Mi, Hlt}),
    .MstRst(MstRst), .ClkInv(ClkInv), .T(control_1_t));
  // Probe on instr_1_regout
  instr instr_1 (
    .Clr(Rst), .Ii(Ii), .BusIn({memory_1_busout, pc_1_busout}), .Io(Io), .Clk(Clk), .BusOut(pc_1_busout),
    .RegOut(instr_1_regout));
  Hex_Digit_Display hex_digit_display_4 (.value(display_1_dispout));  // open: dp

  // Other names for the same wires on the sheet: Mode = in_3; ProgA[11:0] = in_1; ProgD[15:0] = in_4; Speed = in_2
endmodule

module clocks (
  input  ClkMode,
  input  Hlt,
  input  ClkPulse,
  output Clk,
  output ClkInv
);

  wire and_1_out, and_2_out, clock_1_out, or_1_out;

  Clock clock_1 (.out(clock_1_out));
  and and_1 (and_1_out, clock_1_out, ClkMode);
  and and_2 (and_2_out, ~ClkMode, ClkPulse);  // AND_Gate
  or or_1 (or_1_out, and_1_out, and_2_out);
  not not_1 (ClkInv, Clk);
  and and_3 (Clk, or_1_out, ~Hlt);  // AND_Gate
endmodule

module pc (
  input  Jc,
  input  Fc,
  input  Rst,
  input  Jz,
  input  Fz,
  input  J,
  input  Ce,
  input  Clk,
  input  Co,
  input  [11:0] BusIn,
  output [11:0] BusOut
);

  wire and_1_out, and_2_out, or_1_out, or_2_out;
  wire [11:0] counter_1_q;

  and and_1 (and_1_out, Jc, Fc);
  or or_1 (or_1_out, and_1_out, and_2_out);
  and and_2 (and_2_out, Jz, Fz);
  Counter #(.width(12), .max('hfff)) counter_1 (
    .clr(Rst), .load(or_2_out), .up(1'b1), .count(Ce), .clk(Clk), .D(BusIn), .Q(counter_1_q));  // open: carry
  or or_2 (or_2_out, or_1_out, J);
  assign BusOut = Co ? counter_1_q : 12'bz;  // Controlled_Buffer controlled_buffer_1
endmodule

module acc (
  input  [15:0] BusIn,
  input  Xo,
  input  Xi,
  input  Clk,
  input  Clr,
  output [15:0] BusOut,
  output [15:0] RegOut
);

  Register #(.width(16)) register_1 (.D(BusIn), .en(Xi), .clk(Clk), .Q(RegOut), .clr(Clr));
  assign BusOut = Xo ? RegOut : 16'bz;  // Controlled_Buffer controlled_buffer_1
endmodule

module alu (
  input  [15:0] AIn,
  input  Eo,
  input  [15:0] BIn,
  input  Su,
  input  Xr,
  input  An,
  input  Ore,
  input  Nt,
  output [15:0] BusOut,
  output [3:0] Flags
);

  wire adder_1_cout, nor_1_out, not_1_out, subtractor_1_bout;
  wire [15:0] adder_1_out, and_1_out, controlled_buffer_1_out, not_2_out, or_1_out, subtractor_1_out,
       xor_1_out;

  Adder #(.width(16)) adder_1 (.a(AIn), .b(BIn), .out(adder_1_out), .cout(adder_1_cout));  // open: cin
  assign controlled_buffer_1_out = nor_1_out ? adder_1_out : 16'bz;  // Controlled_Buffer controlled_buffer_1
  assign Flags[0] = not_1_out ? adder_1_cout : 1'bz;  // Controlled_Buffer controlled_buffer_2
  Subtractor #(.width(16)) subtractor_1 (
    .a(AIn), .b(BIn), .out(subtractor_1_out), .bout(subtractor_1_bout));  // open: bin
  assign controlled_buffer_1_out = Su ? subtractor_1_out : 16'bz;  // Controlled_Buffer controlled_buffer_3
  not not_1 (not_1_out, Su);
  assign Flags[0] = Su ? subtractor_1_bout : 1'bz;  // Controlled_Buffer controlled_buffer_4
  assign xor_1_out = AIn ^ BIn;  // XOR_Gate xor_1, 16 bits wide
  assign controlled_buffer_1_out = Xr ? xor_1_out : 16'bz;  // Controlled_Buffer controlled_buffer_5
  assign and_1_out = AIn & BIn;  // AND_Gate and_1, 16 bits wide
  assign controlled_buffer_1_out = An ? and_1_out : 16'bz;  // Controlled_Buffer controlled_buffer_6
  assign or_1_out = AIn | BIn;  // OR_Gate or_1, 16 bits wide
  assign controlled_buffer_1_out = Ore ? or_1_out : 16'bz;  // Controlled_Buffer controlled_buffer_7
  assign not_2_out = ~AIn;  // NOT_Gate not_2, 16 bits wide
  assign controlled_buffer_1_out = Nt ? not_2_out : 16'bz;  // Controlled_Buffer controlled_buffer_8
  Adder #(.width(15)) adder_2 (.a(AIn[14:0]), .b(BIn[14:0]), .cout(Flags[3]));  // open: out, cin
  nor nor_1 (nor_1_out, Su, Xr, An, Ore, Nt);
  assign BusOut = Eo ? controlled_buffer_1_out : 16'bz;  // Controlled_Buffer controlled_buffer_9
  BitFinder #(.width(16)) bitfinder_1 (.in(controlled_buffer_1_out), .found(Flags[1]));  // open: index
  BitSelector #(.width(16)) bitselector_1 (.in(controlled_buffer_1_out), .out(Flags[2]), .sel(4'b1111));
endmodule

module flags (
  input  Fo,
  input  [3:0] Flags,
  input  Fi,
  input  Clk,
  input  Rst,
  output [3:0] BusOut,
  output FzO,
  output FcO
);

  wire [3:2] register_1_q;

  Register #(.width(4)) register_1 (.D(Flags), .en(Fi), .clk(Clk), .Q({register_1_q, FzO, FcO}), .clr(Rst));
  assign BusOut = Fo ? {register_1_q, FzO, FcO} : 4'bz;  // Controlled_Buffer controlled_buffer_1
endmodule

module mar (
  input  [11:0] BusIn,
  input  [11:0] ProgIn,
  input  Clk,
  input  Mode,
  input  Clr,
  input  Mi,
  output [11:0] Addr
);

  wire not_1_out, or_1_out;
  wire [11:0] controlled_buffer_1_out;

  Register #(.width(12)) register_1 (.D(controlled_buffer_1_out), .en(or_1_out), .clk(Clk), .Q(Addr), .clr(Clr));
  assign controlled_buffer_1_out = not_1_out ? BusIn : 12'bz;  // Controlled_Buffer controlled_buffer_1
  not not_1 (not_1_out, Mode);
  assign controlled_buffer_1_out = Mode ? ProgIn : 12'bz;  // Controlled_Buffer controlled_buffer_2
  or or_1 (or_1_out, Mode, Mi);
endmodule

module memory (
  input  [11:0] Addr,
  input  Mode,
  input  Prog,
  input  Ri,
  input  Ro,
  input  Clk,
  input  [15:0] BusIn,
  input  [15:0] ProgIn,
  output [15:0] BusOut
);

  wire and_1_out, clock_1_out, controlled_buffer_1_out, not_1_out, not_2_out;
  wire [15:0] controlled_buffer_3_out, ram_1_dout;

  not not_1 (not_1_out, Mode);
  and and_1 (and_1_out, Ri, Clk);
  assign controlled_buffer_1_out = Mode ? Prog : 1'bz;  // Controlled_Buffer controlled_buffer_1
  assign controlled_buffer_1_out = not_1_out ? and_1_out : 1'bz;  // Controlled_Buffer controlled_buffer_2
  assign controlled_buffer_3_out = not_2_out ? BusIn : 16'bz;  // Controlled_Buffer controlled_buffer_3
  not not_2 (not_2_out, Mode);
  assign controlled_buffer_3_out = Mode ? ProgIn : 16'bz;  // Controlled_Buffer controlled_buffer_4
  RAM #(.addrWidth(12), .dataWidth(16), .databus("bibus")) ram_1 (
    .addr(Addr), .we(controlled_buffer_1_out), .oe(1'b1), .clk(clock_1_out), .din(controlled_buffer_3_out),
    .dout(ram_1_dout));
  Clock clock_1 (.out(clock_1_out));
  assign BusOut = Ro ? ram_1_dout : 16'bz;  // Controlled_Buffer controlled_buffer_5
endmodule

module instr (
  input  [15:0] BusIn,
  input  Io,
  input  Ii,
  input  Clk,
  input  Clr,
  output [11:0] BusOut,
  output [3:0] RegOut
);

  wire [11:0] register_1_q;

  Register #(.width(16)) register_1 (.D(BusIn), .en(Ii), .clk(Clk), .Q({RegOut, register_1_q}), .clr(Clr));
  assign BusOut = Io ? register_1_q : 12'bz;  // Controlled_Buffer controlled_buffer_1
endmodule

module control (
  input  [3:0] RegIn,
  input  MstRst,
  input  ClkInv,
  output Rst,
  output [22:0] Ctrls,
  output [2:0] T
);

  Counter #(.width(3), .max('h4)) counter_1 (
    .clr(MstRst), .load(1'b0), .up(1'b1), .count(1'b1), .clk(ClkInv), .Q(T));  // open: D, carry
  ROM #(.addrWidth(7), .dataWidth(23)) rom_1 (.addr({RegIn, T}), .data(Ctrls));

  assign Rst = MstRst;

  // Notes on the sheet:
  //   contents of rom_1 (hex, n*v repeats v):
  //   2002 1028 6*0 2002 1028 12 48 4*0 2002 1028 12 408 8140 0 0 0 2002 1028 12 408 8340 0 0 0 2002 1028
  //   12 84 4*0 2002 1028 50 5*0 2002 1028 4010 5*0 2002 1028 200010 5*0 2002 1028 400010 5*0 2002 1028 12
  //   408 18140 0 0 0 2002 1028 12 408 28140 0 0 0 2002 1028 12 408 8140 0 0 0 2002 1028 12 408 88140 0 0
  //   0 2002 1028 100040 5*0 2002 1028 880 5*0 2002 1028
endmodule

module display (
  input  [15:0] BusIn,
  input  Oi,
  input  Clk,
  input  Clr,
  output [15:0] DispOut
);

  Register #(.width(16)) register_1 (.D(BusIn), .en(Oi), .clk(Clk), .Q(DispOut), .clr(Clr));
endmodule
