// Logisim project ExtraParts.circ as structural Verilog
module ic138 (
  input  in_1,
  input  in_2,
  input  in_3,
  input  in_4,
  input  in_5,
  input  in_6,
  input  in_7,
  input  in_8,
  output out_9,
  output out_10,
  output out_11,
  output out_12,
  output out_13,
  output out_14,
  output out_15,
  output out_16
);

  wire and_1_out, not_1_out, not_2_out, not_3_out, not_4_out, not_5_out, not_6_out, not_7_out, not_8_out;

  not not_1 (not_1_out, in_6);
  not not_2 (not_2_out, not_1_out);
  nand nand_1 (out_9, not_2_out, not_6_out, not_5_out, and_1_out);
  not not_3 (not_3_out, in_8);
  not not_4 (not_4_out, in_7);
  not not_5 (not_5_out, not_4_out);
  not not_6 (not_6_out, not_3_out);
  nand nand_2 (out_10, and_1_out, not_5_out, not_2_out, not_3_out);
  nand nand_3 (out_11, and_1_out, not_6_out, not_2_out, not_4_out);
  nand nand_4 (out_12, and_1_out, not_2_out, not_4_out, not_3_out);
  not not_7 (not_7_out, in_3);
  not not_8 (not_8_out, in_4);
  and and_1 (and_1_out, not_7_out, not_8_out, in_5);
  nand nand_5 (out_13, and_1_out, not_1_out, not_5_out, not_6_out);
  nand nand_6 (out_15, and_1_out, not_1_out, not_4_out, not_6_out);
  nand nand_7 (out_14, and_1_out, not_1_out, not_5_out, not_3_out);
  nand nand_8 (out_16, and_1_out, not_1_out, not_4_out, not_3_out);
endmodule

module ic139 (
  input  in_1,
  input  in_2,
  input  in_3,
  input  in_4,
  input  in_5,
  input  in_6,
  input  in_7,
  input  in_8,
  output out_9,
  output out_10,
  output out_11,
  output out_12,
  output out_13,
  output out_14,
  output out_15,
  output out_16
);

  wire not_1_out, not_2_out, not_3_out, not_4_out, not_5_out, not_6_out, not_7_out, not_8_out, not_9_out;

  nand nand_1 (out_9, not_1_out, not_4_out, not_2_out);
  not not_1 (not_1_out, in_2);
  not not_2 (not_2_out, in_1);
  not not_3 (not_3_out, not_1_out);
  nand nand_2 (out_10, not_2_out, not_4_out, not_3_out);
  nand nand_3 (out_11, not_2_out, not_1_out, not_5_out);
  not not_4 (not_4_out, in_3);
  not not_5 (not_5_out, not_4_out);
  nand nand_4 (out_12, not_2_out, not_5_out, not_3_out);
  nand nand_5 (out_13, not_6_out, not_8_out, in_4);
  not not_6 (not_6_out, in_5);
  not not_7 (not_7_out, not_6_out);
  nand nand_6 (out_15, in_4, not_6_out, not_7_out);
  nand nand_7 (out_14, in_4, not_8_out, not_7_out);
  not not_8 (not_8_out, in_6);
  not not_9 (not_9_out, not_8_out);
  nand nand_8 (out_16, in_4, not_9_out, not_7_out);
endmodule

module ic157 (
  input  in_1,
  input  in_2,
  input  in_3,
  input  in_4,
  input  in_5,
  input  in_6,
  input  in_7,
  input  in_8,
  input  in_9,
  input  in_10,
  input  in_11,
  input  in_12,
  output out_13,
  output out_14,
  output out_15,
  output out_16
);

  wire not_1_out, not_2_out;
  wire [3:0] and_1_out, and_2_out;
  wire [3:3] and_3_out, and_4_out;

  assign and_1_out = {in_9, in_7, in_5, in_3} & {4{and_4_out[3]}};  // AND_Gate and_1, 4 bits wide
  assign and_2_out = {in_10, in_8, in_6, in_4} & {4{and_3_out[3]}};  // AND_Gate and_2, 4 bits wide
  assign {out_13, out_14, out_15, out_16} = and_1_out | and_2_out;  // OR_Gate or_1, 4 bits wide
  not not_1 (not_1_out, in_1);
  not not_2 (not_2_out, in_2);
  and and_3 (and_3_out[3], not_1_out, in_2);
  and and_4 (and_4_out[3], not_1_out, not_2_out);
endmodule

module ic245 (
  input  in_1,
  input  in_2,
  input  in_3,
  input  in_4,
  input  in_5,
  input  in_6,
  input  in_7,
  input  in_8,
  input  in_9,
  input  in_10,
  input  in_11,
  input  in_12,
  input  in_13,
  input  in_14,
  input  in_15,
  input  in_16,
  input  in_17,
  input  in_18,
  output out_19,
  output out_20,
  output out_21,
  output out_22,
  output out_23,
  output out_24,
  output out_25,
  output out_26,
  output out_27,
  output out_28,
  output out_29,
  output out_30,
  output out_31,
  output out_32,
  output out_33,
  output out_34
);

  wire and_1_out, and_2_out, not_1_out, not_2_out, not_3_out;

  not not_1 (not_1_out, in_2);
  and and_1 (and_1_out, not_1_out, in_1);
  assign {out_34, out_33, out_31, out_29, out_27, out_25, out_23, out_21} = and_1_out ? {in_16, in_14, in_12, in_10, in_8, in_6, in_4, in_3} : 8'bz;  // Controlled_Buffer controlled_buffer_1
  not not_2 (not_2_out, in_2);
  not not_3 (not_3_out, in_1);
  and and_2 (and_2_out, not_2_out, not_3_out);
  assign {out_32, out_30, out_28, out_26, out_24, out_22, out_20, out_19} = and_2_out ? {in_18, in_17, in_15, in_13, in_11, in_9, in_7, in_5} : 8'bz;  // Controlled_Buffer controlled_buffer_2
endmodule
