// Logisim project bcd16bit.circ as structural Verilog: 5 circuits, main circuit main
module main (
  input  Set,
  input  [15:0] Data,
  input  Reset,
  input  Decode,
  output [3:0] Ten_Thousands,
  output [3:0] Thousands,
  output [3:0] Hundreds,
  output [3:0] Tens,
  output [3:0] Ones
);

  wire ATmegaClock_out;
  wire [7:0] bcd_32bit_6e2845e8_1_out_7;
  wire [31:0] bcd_32bit_6e2845e8_1_out_8;
  wire [31:16] undriven;

  bcd_32bit_6e2845e8 bcd_32bit_6e2845e8_1 (
    .in_5(Decode), .in_1({undriven, Data}), .in_4(ATmegaClock_out), .in_3(Reset), .in_2(Set),
    .out_8(bcd_32bit_6e2845e8_1_out_8), .out_7(bcd_32bit_6e2845e8_1_out_7));  // open: out_6
  display_bus_18e3c166 BCD_Out (
    .out_8(Ten_Thousands), .out_9(Thousands), .out_10(Hundreds), .out_11(Tens), .out_12(Ones),
    .in_1(bcd_32bit_6e2845e8_1_out_7), .in_2(bcd_32bit_6e2845e8_1_out_8));  // open: out_3, out_4, out_5, out_6, out_7
  Clock ATmegaClock (.out(ATmegaClock_out));
endmodule

module bcd (
  input  in_1,
  input  in_2,
  input  in_3,
  output [3:0] out_4,
  output out_5,
  output out_6,
  output out_7
);

  wire [3:0] rom_1_data;

  ROM #(.addrWidth(4), .dataWidth(4)) rom_1 (.addr({out_4[3:1], in_3}), .data(rom_1_data));
  Register #(.width(4)) register_1 (.D(rom_1_data), .clk(in_2), .Q({out_5, out_4[3:1]}), .clr(in_1));  // open: en

  assign out_4[0] = in_3;
  assign out_6 = in_1;
  assign out_7 = in_2;

  // Notes on the sheet:
  //   contents of rom_1 (hex, n*v repeats v):
  //   0 1 2 3 4 8 9 a b c d e f
endmodule

module bcd_32bit_6e2845e8 (
  input  [31:0] in_1,
  input  in_2,
  input  in_3,
  input  in_4,
  input  in_5,
  output out_6,
  output [7:0] out_7,
  output [31:0] out_8
);

  wire and_1_out, bcd_1_out_5, bcd_1_out_6, bcd_1_out_7, bcd_3_out_5, bcd_3_out_6, bcd_3_out_7, bcd_4_out_5,
       bcd_4_out_6, bcd_4_out_7, bcd_5_out_5, bcd_5_out_6, bcd_5_out_7, bcd_6_out_5, bcd_6_out_6,
       bcd_6_out_7, bcd_7_out_5, bcd_7_out_6, bcd_7_out_7, bcd_8_out_5, bcd_8_out_6, bcd_8_out_7,
       bcd_9_out_5, bcd_9_out_6, bcd_9_out_7, bcd_10_out_5, bcd_10_out_6, bcd_10_out_7, buffer_1_out,
       buffer_2_out, buffer_3_out, counter_1_carry, j_k_ff_1_q, not_2_out, or_1_out, undriven;
  wire [3:0] bcd_1_out_4, bcd_2_out_4, bcd_3_out_4, bcd_4_out_4, bcd_5_out_4, bcd_6_out_4;
  wire [15:0] bcd_8_out_4;

  J_K_Flip_Flop j_k_ff_1 (.J(in_5), .K(not_2_out), .clk(in_4), .Q(j_k_ff_1_q));  // open: Qn, preset, reset
  or or_1 (or_1_out, in_2, and_1_out);
  and and_1 (and_1_out, in_4, out_6, j_k_ff_1_q);
  buf buffer_1 (buffer_1_out, and_1_out);
  Counter #(.width(5), .max('h1f)) counter_1 (
    .clr(in_3), .clk(buffer_1_out), .carry(counter_1_carry));  // open: load, up, count, D, Q
  buf buffer_2 (buffer_2_out, and_1_out);
  bcd bcd_1 (
    .out_4(bcd_1_out_4), .in_3(bcd_4_out_5), .out_5(bcd_1_out_5), .in_1(bcd_4_out_6), .in_2(bcd_4_out_7),
    .out_7(bcd_1_out_7), .out_6(bcd_1_out_6));
  bcd bcd_2 (
    .out_4(bcd_2_out_4), .in_3(bcd_1_out_5), .in_1(bcd_1_out_6), .in_2(bcd_1_out_7));  // open: out_5, out_7, out_6
  not not_1 (out_6, counter_1_carry);
  not not_2 (not_2_out, out_6);
  Pull_Resistor pull_resistor_1 (.node(out_7));
  assign out_7 = not_2_out ? {bcd_2_out_4, bcd_1_out_4} : 8'bz;  // Controlled_Buffer controlled_buffer_1
  bcd bcd_3 (
    .out_4(bcd_3_out_4), .in_3(bcd_7_out_5), .out_5(bcd_3_out_5), .in_1(bcd_7_out_6), .in_2(bcd_7_out_7),
    .out_7(bcd_3_out_7), .out_6(bcd_3_out_6));
  bcd bcd_4 (
    .out_4(bcd_4_out_4), .in_3(bcd_6_out_5), .out_5(bcd_4_out_5), .in_1(bcd_6_out_6), .in_2(bcd_6_out_7),
    .out_7(bcd_4_out_7), .out_6(bcd_4_out_6));
  bcd bcd_5 (
    .out_4(bcd_5_out_4), .in_3(bcd_3_out_5), .out_5(bcd_5_out_5), .in_1(bcd_3_out_6), .in_2(bcd_3_out_7),
    .out_7(bcd_5_out_7), .out_6(bcd_5_out_6));
  bcd bcd_6 (
    .out_4(bcd_6_out_4), .in_3(bcd_5_out_5), .out_5(bcd_6_out_5), .in_1(bcd_5_out_6), .in_2(bcd_5_out_7),
    .out_7(bcd_6_out_7), .out_6(bcd_6_out_6));
  assign out_8 = not_2_out ? {bcd_4_out_4, bcd_6_out_4, bcd_5_out_4, bcd_3_out_4, bcd_8_out_4} : 32'bz;  // Controlled_Buffer controlled_buffer_2
  Pull_Resistor pull_resistor_2 (.node(out_8));
  bcd bcd_7 (
    .out_4(bcd_8_out_4[15:12]), .in_3(bcd_9_out_5), .out_5(bcd_7_out_5), .in_1(bcd_9_out_6),
    .in_2(bcd_9_out_7), .out_7(bcd_7_out_7), .out_6(bcd_7_out_6));
  bcd bcd_8 (
    .out_4(bcd_8_out_4[3:0]), .in_3(undriven), .out_5(bcd_8_out_5), .in_1(in_3), .in_2(buffer_2_out),
    .out_7(bcd_8_out_7), .out_6(bcd_8_out_6));
  bcd bcd_9 (
    .out_4(bcd_8_out_4[11:8]), .in_3(bcd_10_out_5), .out_5(bcd_9_out_5), .in_1(bcd_10_out_6),
    .in_2(bcd_10_out_7), .out_7(bcd_9_out_7), .out_6(bcd_9_out_6));
  bcd bcd_10 (
    .out_4(bcd_8_out_4[7:4]), .in_3(bcd_8_out_5), .out_5(bcd_10_out_5), .in_1(bcd_8_out_6),
    .in_2(bcd_8_out_7), .out_7(bcd_10_out_7), .out_6(bcd_10_out_6));
  buf buffer_3 (buffer_3_out, in_2);
  // Shift_Register #(.length(32)) shift_register_1: pin names not known; wires that end beside it: in_3, buffer_3_out, 1'b1, or_1_out, 1'b0, in_1[0], in_1[1], in_1[2], in_1[3], in_1[4], in_1[5], in_1[6], in_1[7], in_1[8], in_1[9], in_1[10], in_1[11]
endmodule

module decoder_display_b0496809 (
  input  [3:0] in_1,
  output [6:0] out_2,
  output [6:0] out_3,
  output [6:0] out_4,
  output [6:0] out_5
);

  wire [31:28] rom_1_data;

  ROM #(.addrWidth(4), .dataWidth(32)) rom_1 (.addr(in_1), .data({rom_1_data, out_2, out_3, out_4, out_5}));

  // Notes on the sheet:
  //   contents of rom_1 (hex, n*v repeats v):
  //   ff060ff 7f 9f264f9 93264ff f02047f f3264cf ff264cf 810207f ff264ff f3264ff
endmodule

module display_bus_18e3c166 (
  input  [7:0] in_1,
  input  [31:0] in_2,
  output [3:0] out_3,
  output [3:0] out_4,
  output [3:0] out_5,
  output [3:0] out_6,
  output [3:0] out_7,
  output [3:0] out_8,
  output [3:0] out_9,
  output [3:0] out_10,
  output [3:0] out_11,
  output [3:0] out_12
);


  assign out_3 = in_1[7:4];
  assign out_4 = in_1[3:0];
  assign out_5 = in_2[31:28];
  assign out_6 = in_2[27:24];
  assign out_7 = in_2[23:20];
  assign out_8 = in_2[19:16];
  assign out_9 = in_2[15:12];
  assign out_10 = in_2[11:8];
  assign out_11 = in_2[7:4];
  assign out_12 = in_2[3:0];
endmodule
